// Logisim project arithmetic-right.circ as structural Verilog: 1 circuit, main circuit main
module main (
  input  [7:0] A,
  input  [7:0] B,
  input  [2:0] OP,
  output C,
  output [7:0] Y,
  output Z
);

  wire n5, n8, n36, n37, n38, n39, n40, n41, n44, n46;
  wire [7:0] n4, n7, n19, n20, n21, n22, n26, n27, n28, n29, n30, n31;

  Adder #(.width(8)) adder_1 (.a(A), .b(B), .out(n4), .cin(1'b0), .cout(n5));
  Subtractor #(.width(8)) subtractor_1 (.a(A), .b(B), .out(n7), .bin(1'b0), .bout(n8));
  assign n19 = A & B;  // AND_Gate and_1, 8 bits wide
  assign n20 = A | B;  // OR_Gate or_1, 8 bits wide
  assign n21 = A ^ B;  // XOR_Gate xor_1, 8 bits wide
  assign n22 = ~A;  // NOT_Gate not_1, 8 bits wide
  Multiplexer #(.width(8), .select(1), .enable("false")) multiplexer_1 (.in0(n4), .in1(n7), .out(n26), .sel(OP[0]));
  Multiplexer #(.width(8), .select(1), .enable("false")) multiplexer_2 (.in0(n19), .in1(n20), .out(n27), .sel(OP[0]));
  Multiplexer #(.width(8), .select(1), .enable("false")) multiplexer_3 (.in0(n21), .in1(n22), .out(n28), .sel(OP[0]));
  Multiplexer #(.width(8), .select(1), .enable("false")) multiplexer_4 (
    .in0({A[6:0], 1'b0}), .in1({{2{A[7]}}, A[6:1]}), .out(n29), .sel(OP[0]));
  Multiplexer #(.width(8), .select(1), .enable("false")) multiplexer_5 (.in0(n26), .in1(n27), .out(n30), .sel(OP[1]));
  Multiplexer #(.width(8), .select(1), .enable("false")) multiplexer_6 (.in0(n28), .in1(n29), .out(n31), .sel(OP[1]));
  Multiplexer #(.width(8), .select(1), .enable("false")) multiplexer_7 (.in0(n30), .in1(n31), .out(Y), .sel(OP[2]));
  Multiplexer #(.width(1), .select(1), .enable("false")) multiplexer_8 (.in0(n5), .in1(n8), .out(n36), .sel(OP[0]));
  Multiplexer #(.width(1), .select(1), .enable("false")) multiplexer_9 (.in0(1'b0), .in1(1'b0), .out(n37), .sel(OP[0]));
  Multiplexer #(.width(1), .select(1), .enable("false")) multiplexer_10 (
    .in0(1'b0), .in1(1'b0), .out(n38), .sel(OP[0]));
  Multiplexer #(.width(1), .select(1), .enable("false")) multiplexer_11 (
    .in0(A[7]), .in1(A[0]), .out(n39), .sel(OP[0]));
  Multiplexer #(.width(1), .select(1), .enable("false")) multiplexer_12 (.in0(n36), .in1(n37), .out(n40), .sel(OP[1]));
  Multiplexer #(.width(1), .select(1), .enable("false")) multiplexer_13 (.in0(n38), .in1(n39), .out(n41), .sel(OP[1]));
  Multiplexer #(.width(1), .select(1), .enable("false")) multiplexer_14 (.in0(n40), .in1(n41), .out(C), .sel(OP[2]));
  Comparator #(.width(8), .mode("unsigned")) comparator_1 (.a(Y), .b({8{1'b0}}), .gt(n44), .eq(Z), .lt(n46));

  // Other names for the same wires on the sheet: n9 = A[0]; n17[7:1] = A[6:0]; n10 = A[1];
  //   n18[7:0] = {{2{A[7]}}, A[6:1]}; n11 = A[2]; n12 = A[3]; n13 = A[4]; n14 = A[5]; n15 = A[6]; n16 = A[7];
  //   n32[7:0] = Y; n42 = C; n45 = Z; n23 = OP[0]; n33 = OP[0]; n24 = OP[1]; n34 = OP[1]; n25 = OP[2]; n35 = OP[2]
endmodule
