// Logisim project reference.circ as structural Verilog: 1 circuit, main circuit main
module main (
  input  CLK,
  input  RST,
  output [3:0] Q
);

  wire [3:0] Dsync, Qp1;

  Adder #(.width(4)) adder_1 (.a(Q), .b(4'b0001), .out(Qp1), .cin(1'b0));  // open: cout
  Register #(.width(4), .trigger("rising"), .Select("high")) u_Q (
    .D(Dsync), .en(1'b1), .Q(Q), .clk(CLK), .clr(1'b0), .cs(1'b1), .preset(1'b0));
  Multiplexer #(.width(4), .select(1), .enable("false")) multiplexer_1 (
    .in0(Qp1), .in1(4'b0000), .out(Dsync), .sel(RST));
endmodule
