// Logisim project reference.circ as structural Verilog: 1 circuit, main circuit main
module main (
  input  CLK,
  input  RST,
  input  [15:0] INST,
  input  [3:0] MA,
  input  [2:0] IRQ,
  output [7:0] PC,
  output IE,
  output HALTED,
  output [2:0] MASK,
  output [7:0] R0,
  output [2:0] PENDING,
  output [7:0] R1,
  output [1:0] LEVEL,
  output [7:0] R2,
  output [1:0] DEPTH,
  output [7:0] R3,
  output [7:0] EPC,
  output [7:0] MD,
  output [2:0] ACK
);

  wire n30, n32, n33, n34, n35, n36, n37, n38, n40, n41, n42, n43, n44, n45, n46, n48, n49, n50, n51, n52,
       n53, n54, n55, n56, n57, n58, n59, n60, n61, n62, n63, n64, n76, n77, n78, n79, n80, n81, n85, n89,
       n90, n91, n92, n94, n95, n96, n98, n99, n100, n102, n103, n104, n108, n109, n110, n111, n112, n113,
       n114, n115, n116, n117, n118, n119, n120, n123, n125, n126, n127, n128, n131, n134, n135, n136, n137,
       n140, n141, n142, n143, n144, n147, n150, n151, n152, n153, n156, n157, n158, n159, n160, n163, n166,
       n167, n168, n169, n172, n185, n186, n187, n194, n196, n199, n202, n203, n204, n205, n206, n207, n208,
       n212, n264, n266, n300, n301, n302, n304, n305, n306, n308, n309, n310, n312, n313, n314, n316, n317,
       n318, n320, n321, n322, n324, n325, n326, n328, n329, n330, n332, n333, n334, n336, n337, n338, n340,
       n341, n342, n344, n345, n346, n348, n349, n350, n352, n353, n354, n356, n357, n358, n360, n361, n362,
       n363, n364, n365, n366, n367, n368, n369, n370, n371, n372, n373, n374, n375, n376, n377, n378, n379,
       n381, n382, n383, n384, n385, n387, n388, n389, n390, n391, n393, n394, n395, n396, n397, n399, n400,
       n401, n402, n403, n404, n406, n407, n408, n409, n410, n412, n413, n414, n415, n416, n418, n419, n420,
       n421, n422, n424, n425, n426, n427, n428, n430, n431, n432, n433, n434, n436, n437, n438, n439, n440,
       n442, n443, n444, n445, n446, n448, n449, n450, n451, n452, n454, n455, n456, n457, n458, n460, n461,
       n462, n463, n464, n466, n467, n468, n469, n470, n472, n473, n474, n475, n476, n478, n479, n480, n481,
       n482, n484, n485, n486, n487, n488, n490, n491, n492, n493, n494, n496, n497, n498, n499, n500, n501,
       n502, n503, n504, n506, n508, n509, n511, n512, n513, n514, n516, n517, n518;
  wire [1:0] n67, n70, n73, n138, n139, n154, n155, n170, n171, n190, n191, n192, n193, n195, n197, n198,
       n200, n201;
  wire [2:0] n84, n88, n132, n133, n148, n149, n164, n165, n180, n181, n182, n209, n210, n211;
  wire [7:0] mem0, mem1, mem2, mem3, mem4, mem5, mem6, mem7, mem8, mem9, mem10, mem11, mem12, mem13, mem14,
       mem15, n69, n72, n75, n122, n124, n129, n130, n145, n146, n161, n162, n175, n176, n213, n236, n237,
       n238, n241, n242, n243, n248, n249, n250, n251, n252, n253, n254, n255, n256, n257, n258, n259, n260,
       n261, n262, n263, n265, n277, n278, n279, n284, n285, n286, n287, n288, n289, n290, n291, n292, n293,
       n294, n295, n296, n297, n298, n380, n386, n392, n398, n405, n411, n417, n423, n429, n435, n441, n447,
       n453, n459, n465, n471, n477, n483, n489, n495, n505, n507, n510, n515, n523, n524, n525, n526, n527,
       n528, n529, n530, n531, n532, n533, n534, n535, n536;

  or or_1 (n30, PENDING[0], IRQ[0]);
  Comparator #(.width(2), .mode("unsigned")) comparator_1 (.a(LEVEL), .b(2'b01), .gt(n32), .eq(n33), .lt(n34));
  and and_1 (n35, n30, n34);
  and and_2 (n36, n35, IE);
  and and_3 (n37, n36, MASK[0]);
  or or_2 (n38, PENDING[1], IRQ[1]);
  Comparator #(.width(2), .mode("unsigned")) comparator_2 (.a(LEVEL), .b(2'b10), .gt(n40), .eq(n41), .lt(n42));
  and and_4 (n43, n38, n42);
  and and_5 (n44, n43, IE);
  and and_6 (n45, n44, MASK[1]);
  or or_3 (n46, PENDING[2], IRQ[2]);
  Comparator #(.width(2), .mode("unsigned")) comparator_3 (.a(LEVEL), .b(2'b11), .gt(n48), .eq(n49), .lt(n50));
  and and_7 (n51, n46, n50);
  and and_8 (n52, n51, IE);
  and and_9 (n53, n52, MASK[2]);
  not not_1 (n54, 1'b0);
  and and_10 (n55, n53, n54);
  or or_4 (n56, 1'b0, n53);
  not not_2 (n57, n56);
  and and_11 (n58, n45, n57);
  or or_5 (n59, n56, n45);
  not not_3 (n60, n59);
  and and_12 (n61, n37, n60);
  or or_6 (n62, n59, n37);
  or or_7 (n63, n61, n58);
  or or_8 (n64, n63, n55);
  Multiplexer #(.width(2), .select(1), .enable("false")) multiplexer_1 (.in0(2'b00), .in1(2'b01), .out(n67), .sel(n61));
  Multiplexer #(.width(8), .select(1), .enable("false")) multiplexer_2 (
    .in0({8{1'b0}}), .in1(8'h80), .out(n69), .sel(n61));
  Multiplexer #(.width(2), .select(1), .enable("false")) multiplexer_3 (.in0(n67), .in1(2'b10), .out(n70), .sel(n58));
  Multiplexer #(.width(8), .select(1), .enable("false")) multiplexer_4 (.in0(n69), .in1(8'ha0), .out(n72), .sel(n58));
  Multiplexer #(.width(2), .select(1), .enable("false")) multiplexer_5 (.in0(n70), .in1(2'b11), .out(n73), .sel(n55));
  Multiplexer #(.width(8), .select(1), .enable("false")) multiplexer_6 (.in0(n72), .in1(8'hc0), .out(n75), .sel(n55));
  not not_4 (n76, n61);
  and and_13 (n77, n30, n76);
  not not_5 (n78, n58);
  and and_14 (n79, n38, n78);
  not not_6 (n80, n55);
  and and_15 (n81, n46, n80);
  Multiplexer #(.width(3), .select(1), .enable("false")) multiplexer_7 (
    .in0({n81, n79, n77}), .in1(3'b000), .out(n84), .sel(RST));
  or or_9 (n85, RST, 1'b1);
  Register #(.width(3), .trigger("rising"), .Select("high")) register_1 (
    .D(n84), .en(n85), .Q(PENDING), .clk(CLK), .clr(1'b0), .cs(1'b1), .preset(1'b0));
  Multiplexer #(.width(3), .select(1), .enable("false")) multiplexer_8 (
    .in0({n55, n58, n61}), .in1(3'b000), .out(n88), .sel(RST));
  or or_10 (n89, RST, 1'b1);
  Register #(.width(3), .trigger("rising"), .Select("high")) register_2 (
    .D(n88), .en(n89), .Q(ACK), .clk(CLK), .clr(1'b0), .cs(1'b1), .preset(1'b0));
  not not_7 (n90, HALTED);
  not not_8 (n91, n64);
  and and_16 (n92, n90, n91);
  Comparator #(.width(16), .mode("unsigned")) comparator_4 (.a(INST), .b(16'h1), .gt(n94), .eq(n95), .lt(n96));
  Comparator #(.width(16), .mode("unsigned")) comparator_5 (.a(INST), .b(16'h2), .gt(n98), .eq(n99), .lt(n100));
  Comparator #(.width(16), .mode("unsigned")) comparator_6 (.a(INST), .b(16'h3), .gt(n102), .eq(n103), .lt(n104));
  Comparator #(.width(13), .mode("unsigned")) comparator_7 (.a(INST[15:3]), .b(13'h2), .gt(n108), .eq(n109), .lt(n110));
  and and_17 (n111, n92, n109);
  and and_18 (n112, n92, n95);
  and and_19 (n113, n92, n99);
  Comparator #(.width(2), .mode("unsigned")) comparator_8 (.a(DEPTH), .b(2'b00), .gt(n114), .eq(n115), .lt(n116));
  not not_9 (n117, n115);
  and and_20 (n118, n92, n103);
  and and_21 (n119, n118, n117);
  or or_11 (n120, n64, n119);
  Adder #(.width(8)) adder_1 (.a(PC), .b(8'h1), .out(n122), .cin(1'b0), .cout(n123));
  Multiplexer #(.width(8), .select(1), .enable("false")) multiplexer_9 (.in0(PC), .in1(n122), .out(n124), .sel(HALTED));
  Comparator #(.width(2), .mode("unsigned")) comparator_9 (.a(DEPTH), .b(2'b00), .gt(n125), .eq(n126), .lt(n127));
  and and_22 (n128, n64, n126);
  Multiplexer #(.width(8), .select(1), .enable("false")) multiplexer_10 (
    .in0(n124), .in1({8{1'b0}}), .out(n130), .sel(RST));
  or or_12 (n131, RST, n128);
  Register #(.width(8), .trigger("rising"), .Select("high")) register_3 (
    .D(n130), .en(n131), .Q(n129), .clk(CLK), .clr(1'b0), .cs(1'b1), .preset(1'b0));
  Multiplexer #(.width(3), .select(1), .enable("false")) multiplexer_11 (
    .in0(MASK), .in1(3'b000), .out(n133), .sel(RST));
  or or_13 (n134, RST, n128);
  Register #(.width(3), .trigger("rising"), .Select("high")) register_4 (
    .D(n133), .en(n134), .Q(n132), .clk(CLK), .clr(1'b0), .cs(1'b1), .preset(1'b0));
  Multiplexer #(.width(1), .select(1), .enable("false")) multiplexer_12 (.in0(IE), .in1(1'b0), .out(n136), .sel(RST));
  or or_14 (n137, RST, n128);
  Register #(.width(1), .trigger("rising"), .Select("high")) register_5 (
    .D(n136), .en(n137), .Q(n135), .clk(CLK), .clr(1'b0), .cs(1'b1), .preset(1'b0));
  Multiplexer #(.width(2), .select(1), .enable("false")) multiplexer_13 (
    .in0(LEVEL), .in1(2'b00), .out(n139), .sel(RST));
  or or_15 (n140, RST, n128);
  Register #(.width(2), .trigger("rising"), .Select("high")) register_6 (
    .D(n139), .en(n140), .Q(n138), .clk(CLK), .clr(1'b0), .cs(1'b1), .preset(1'b0));
  Comparator #(.width(2), .mode("unsigned")) comparator_10 (.a(DEPTH), .b(2'b01), .gt(n141), .eq(n142), .lt(n143));
  and and_23 (n144, n64, n142);
  Multiplexer #(.width(8), .select(1), .enable("false")) multiplexer_14 (
    .in0(n124), .in1({8{1'b0}}), .out(n146), .sel(RST));
  or or_16 (n147, RST, n144);
  Register #(.width(8), .trigger("rising"), .Select("high")) register_7 (
    .D(n146), .en(n147), .Q(n145), .clk(CLK), .clr(1'b0), .cs(1'b1), .preset(1'b0));
  Multiplexer #(.width(3), .select(1), .enable("false")) multiplexer_15 (
    .in0(MASK), .in1(3'b000), .out(n149), .sel(RST));
  or or_17 (n150, RST, n144);
  Register #(.width(3), .trigger("rising"), .Select("high")) register_8 (
    .D(n149), .en(n150), .Q(n148), .clk(CLK), .clr(1'b0), .cs(1'b1), .preset(1'b0));
  Multiplexer #(.width(1), .select(1), .enable("false")) multiplexer_16 (.in0(IE), .in1(1'b0), .out(n152), .sel(RST));
  or or_18 (n153, RST, n144);
  Register #(.width(1), .trigger("rising"), .Select("high")) register_9 (
    .D(n152), .en(n153), .Q(n151), .clk(CLK), .clr(1'b0), .cs(1'b1), .preset(1'b0));
  Multiplexer #(.width(2), .select(1), .enable("false")) multiplexer_17 (
    .in0(LEVEL), .in1(2'b00), .out(n155), .sel(RST));
  or or_19 (n156, RST, n144);
  Register #(.width(2), .trigger("rising"), .Select("high")) register_10 (
    .D(n155), .en(n156), .Q(n154), .clk(CLK), .clr(1'b0), .cs(1'b1), .preset(1'b0));
  Comparator #(.width(2), .mode("unsigned")) comparator_11 (.a(DEPTH), .b(2'b10), .gt(n157), .eq(n158), .lt(n159));
  and and_24 (n160, n64, n158);
  Multiplexer #(.width(8), .select(1), .enable("false")) multiplexer_18 (
    .in0(n124), .in1({8{1'b0}}), .out(n162), .sel(RST));
  or or_20 (n163, RST, n160);
  Register #(.width(8), .trigger("rising"), .Select("high")) register_11 (
    .D(n162), .en(n163), .Q(n161), .clk(CLK), .clr(1'b0), .cs(1'b1), .preset(1'b0));
  Multiplexer #(.width(3), .select(1), .enable("false")) multiplexer_19 (
    .in0(MASK), .in1(3'b000), .out(n165), .sel(RST));
  or or_21 (n166, RST, n160);
  Register #(.width(3), .trigger("rising"), .Select("high")) register_12 (
    .D(n165), .en(n166), .Q(n164), .clk(CLK), .clr(1'b0), .cs(1'b1), .preset(1'b0));
  Multiplexer #(.width(1), .select(1), .enable("false")) multiplexer_20 (.in0(IE), .in1(1'b0), .out(n168), .sel(RST));
  or or_22 (n169, RST, n160);
  Register #(.width(1), .trigger("rising"), .Select("high")) register_13 (
    .D(n168), .en(n169), .Q(n167), .clk(CLK), .clr(1'b0), .cs(1'b1), .preset(1'b0));
  Multiplexer #(.width(2), .select(1), .enable("false")) multiplexer_21 (
    .in0(LEVEL), .in1(2'b00), .out(n171), .sel(RST));
  or or_23 (n172, RST, n160);
  Register #(.width(2), .trigger("rising"), .Select("high")) register_14 (
    .D(n171), .en(n172), .Q(n170), .clk(CLK), .clr(1'b0), .cs(1'b1), .preset(1'b0));
  Multiplexer #(.width(8), .select(1), .enable("false")) multiplexer_22 (
    .in0({8{1'b0}}), .in1(n129), .out(n175), .sel(DEPTH[0]));
  Multiplexer #(.width(8), .select(1), .enable("false")) multiplexer_23 (
    .in0(n145), .in1(n161), .out(n176), .sel(DEPTH[0]));
  Multiplexer #(.width(8), .select(1), .enable("false")) multiplexer_24 (
    .in0(n175), .in1(n176), .out(EPC), .sel(DEPTH[1]));
  Multiplexer #(.width(3), .select(1), .enable("false")) multiplexer_25 (
    .in0(3'b000), .in1(n132), .out(n180), .sel(DEPTH[0]));
  Multiplexer #(.width(3), .select(1), .enable("false")) multiplexer_26 (
    .in0(n148), .in1(n164), .out(n181), .sel(DEPTH[0]));
  Multiplexer #(.width(3), .select(1), .enable("false")) multiplexer_27 (
    .in0(n180), .in1(n181), .out(n182), .sel(DEPTH[1]));
  Multiplexer #(.width(1), .select(1), .enable("false")) multiplexer_28 (
    .in0(1'b0), .in1(n135), .out(n185), .sel(DEPTH[0]));
  Multiplexer #(.width(1), .select(1), .enable("false")) multiplexer_29 (
    .in0(n151), .in1(n167), .out(n186), .sel(DEPTH[0]));
  Multiplexer #(.width(1), .select(1), .enable("false")) multiplexer_30 (
    .in0(n185), .in1(n186), .out(n187), .sel(DEPTH[1]));
  Multiplexer #(.width(2), .select(1), .enable("false")) multiplexer_31 (
    .in0(2'b00), .in1(n138), .out(n190), .sel(DEPTH[0]));
  Multiplexer #(.width(2), .select(1), .enable("false")) multiplexer_32 (
    .in0(n154), .in1(n170), .out(n191), .sel(DEPTH[0]));
  Multiplexer #(.width(2), .select(1), .enable("false")) multiplexer_33 (
    .in0(n190), .in1(n191), .out(n192), .sel(DEPTH[1]));
  Adder #(.width(2)) adder_2 (.a(DEPTH), .b(2'b01), .out(n193), .cin(1'b0), .cout(n194));
  Subtractor #(.width(2)) subtractor_1 (.a(DEPTH), .b(2'b01), .out(n195), .bin(1'b0), .bout(n196));
  Multiplexer #(.width(2), .select(1), .enable("false")) multiplexer_34 (.in0(n195), .in1(n193), .out(n197), .sel(n64));
  Multiplexer #(.width(2), .select(1), .enable("false")) multiplexer_35 (
    .in0(n197), .in1(2'b00), .out(n198), .sel(RST));
  or or_24 (n199, RST, n120);
  Register #(.width(2), .trigger("rising"), .Select("high")) register_15 (
    .D(n198), .en(n199), .Q(DEPTH), .clk(CLK), .clr(1'b0), .cs(1'b1), .preset(1'b0));
  Multiplexer #(.width(2), .select(1), .enable("false")) multiplexer_36 (.in0(n192), .in1(n73), .out(n200), .sel(n64));
  Multiplexer #(.width(2), .select(1), .enable("false")) multiplexer_37 (
    .in0(n200), .in1(2'b00), .out(n201), .sel(RST));
  or or_25 (n202, RST, n120);
  Register #(.width(2), .trigger("rising"), .Select("high")) register_16 (
    .D(n201), .en(n202), .Q(LEVEL), .clk(CLK), .clr(1'b0), .cs(1'b1), .preset(1'b0));
  Multiplexer #(.width(1), .select(1), .enable("false")) multiplexer_38 (.in0(IE), .in1(1'b1), .out(n203), .sel(n112));
  Multiplexer #(.width(1), .select(1), .enable("false")) multiplexer_39 (
    .in0(n203), .in1(1'b0), .out(n204), .sel(n113));
  Multiplexer #(.width(1), .select(1), .enable("false")) multiplexer_40 (
    .in0(n204), .in1(n187), .out(n205), .sel(n119));
  Multiplexer #(.width(1), .select(1), .enable("false")) multiplexer_41 (.in0(n205), .in1(1'b0), .out(n206), .sel(n64));
  Multiplexer #(.width(1), .select(1), .enable("false")) multiplexer_42 (.in0(n206), .in1(1'b0), .out(n207), .sel(RST));
  or or_26 (n208, RST, 1'b1);
  Register #(.width(1), .trigger("rising"), .Select("high")) register_17 (
    .D(n207), .en(n208), .Q(IE), .clk(CLK), .clr(1'b0), .cs(1'b1), .preset(1'b0));
  Multiplexer #(.width(3), .select(1), .enable("false")) multiplexer_43 (
    .in0(MASK), .in1(INST[2:0]), .out(n209), .sel(n111));
  Multiplexer #(.width(3), .select(1), .enable("false")) multiplexer_44 (
    .in0(n209), .in1(n182), .out(n210), .sel(n119));
  Multiplexer #(.width(3), .select(1), .enable("false")) multiplexer_45 (
    .in0(n210), .in1(3'b000), .out(n211), .sel(RST));
  or or_27 (n212, RST, 1'b1);
  Register #(.width(3), .trigger("rising"), .Select("high")) register_18 (
    .D(n211), .en(n212), .Q(MASK), .clk(CLK), .clr(1'b0), .cs(1'b1), .preset(1'b0));
  Multiplexer #(.width(8), .select(1), .enable("false")) multiplexer_46 (.in0(EPC), .in1(n75), .out(n213), .sel(n64));
  Multiplexer #(.width(8), .select(1), .enable("false")) multiplexer_47 (
    .in0(R0), .in1(R1), .out(n236), .sel(INST[10]));
  Multiplexer #(.width(8), .select(1), .enable("false")) multiplexer_48 (
    .in0(R2), .in1(R3), .out(n237), .sel(INST[10]));
  Multiplexer #(.width(8), .select(1), .enable("false")) multiplexer_49 (
    .in0(n236), .in1(n237), .out(n238), .sel(INST[11]));
  Multiplexer #(.width(8), .select(1), .enable("false")) multiplexer_50 (.in0(R0), .in1(R1), .out(n241), .sel(INST[8]));
  Multiplexer #(.width(8), .select(1), .enable("false")) multiplexer_51 (.in0(R2), .in1(R3), .out(n242), .sel(INST[8]));
  Multiplexer #(.width(8), .select(1), .enable("false")) multiplexer_52 (
    .in0(n241), .in1(n242), .out(n243), .sel(INST[9]));
  Multiplexer #(.width(8), .select(1), .enable("false")) multiplexer_53 (
    .in0(mem0), .in1(mem1), .out(n248), .sel(INST[0]));
  Multiplexer #(.width(8), .select(1), .enable("false")) multiplexer_54 (
    .in0(mem2), .in1(mem3), .out(n249), .sel(INST[0]));
  Multiplexer #(.width(8), .select(1), .enable("false")) multiplexer_55 (
    .in0(mem4), .in1(mem5), .out(n250), .sel(INST[0]));
  Multiplexer #(.width(8), .select(1), .enable("false")) multiplexer_56 (
    .in0(mem6), .in1(mem7), .out(n251), .sel(INST[0]));
  Multiplexer #(.width(8), .select(1), .enable("false")) multiplexer_57 (
    .in0(mem8), .in1(mem9), .out(n252), .sel(INST[0]));
  Multiplexer #(.width(8), .select(1), .enable("false")) multiplexer_58 (
    .in0(mem10), .in1(mem11), .out(n253), .sel(INST[0]));
  Multiplexer #(.width(8), .select(1), .enable("false")) multiplexer_59 (
    .in0(mem12), .in1(mem13), .out(n254), .sel(INST[0]));
  Multiplexer #(.width(8), .select(1), .enable("false")) multiplexer_60 (
    .in0(mem14), .in1(mem15), .out(n255), .sel(INST[0]));
  Multiplexer #(.width(8), .select(1), .enable("false")) multiplexer_61 (
    .in0(n248), .in1(n249), .out(n256), .sel(INST[1]));
  Multiplexer #(.width(8), .select(1), .enable("false")) multiplexer_62 (
    .in0(n250), .in1(n251), .out(n257), .sel(INST[1]));
  Multiplexer #(.width(8), .select(1), .enable("false")) multiplexer_63 (
    .in0(n252), .in1(n253), .out(n258), .sel(INST[1]));
  Multiplexer #(.width(8), .select(1), .enable("false")) multiplexer_64 (
    .in0(n254), .in1(n255), .out(n259), .sel(INST[1]));
  Multiplexer #(.width(8), .select(1), .enable("false")) multiplexer_65 (
    .in0(n256), .in1(n257), .out(n260), .sel(INST[2]));
  Multiplexer #(.width(8), .select(1), .enable("false")) multiplexer_66 (
    .in0(n258), .in1(n259), .out(n261), .sel(INST[2]));
  Multiplexer #(.width(8), .select(1), .enable("false")) multiplexer_67 (
    .in0(n260), .in1(n261), .out(n262), .sel(INST[3]));
  Adder #(.width(8)) adder_3 (.a(n238), .b(n243), .out(n263), .cin(1'b0), .cout(n264));
  Subtractor #(.width(8)) subtractor_2 (.a(n238), .b(n243), .out(n265), .bin(1'b0), .bout(n266));
  assign n277 = n238 ^ n243;  // XOR_Gate xor_1, 8 bits wide
  assign n278 = n238 & n243;  // AND_Gate and_25, 8 bits wide
  assign n279 = n238 | n243;  // OR_Gate or_28, 8 bits wide
  Multiplexer #(.width(8), .select(1), .enable("false")) multiplexer_68 (
    .in0({8{1'b0}}), .in1(INST[7:0]), .out(n284), .sel(INST[12]));
  Multiplexer #(.width(8), .select(1), .enable("false")) multiplexer_69 (
    .in0(n243), .in1(n263), .out(n285), .sel(INST[12]));
  Multiplexer #(.width(8), .select(1), .enable("false")) multiplexer_70 (
    .in0(n265), .in1(n277), .out(n286), .sel(INST[12]));
  Multiplexer #(.width(8), .select(1), .enable("false")) multiplexer_71 (
    .in0(n278), .in1(n279), .out(n287), .sel(INST[12]));
  Multiplexer #(.width(8), .select(1), .enable("false")) multiplexer_72 (
    .in0({n238[6:0], 1'b0}), .in1({1'b0, n238[7:1]}), .out(n288), .sel(INST[12]));
  Multiplexer #(.width(8), .select(1), .enable("false")) multiplexer_73 (
    .in0(n262), .in1({8{1'b0}}), .out(n289), .sel(INST[12]));
  Multiplexer #(.width(8), .select(1), .enable("false")) multiplexer_74 (
    .in0({8{1'b0}}), .in1({8{1'b0}}), .out(n290), .sel(INST[12]));
  Multiplexer #(.width(8), .select(1), .enable("false")) multiplexer_75 (
    .in0({8{1'b0}}), .in1({8{1'b0}}), .out(n291), .sel(INST[12]));
  Multiplexer #(.width(8), .select(1), .enable("false")) multiplexer_76 (
    .in0(n284), .in1(n285), .out(n292), .sel(INST[13]));
  Multiplexer #(.width(8), .select(1), .enable("false")) multiplexer_77 (
    .in0(n286), .in1(n287), .out(n293), .sel(INST[13]));
  Multiplexer #(.width(8), .select(1), .enable("false")) multiplexer_78 (
    .in0(n288), .in1(n289), .out(n294), .sel(INST[13]));
  Multiplexer #(.width(8), .select(1), .enable("false")) multiplexer_79 (
    .in0(n290), .in1(n291), .out(n295), .sel(INST[13]));
  Multiplexer #(.width(8), .select(1), .enable("false")) multiplexer_80 (
    .in0(n292), .in1(n293), .out(n296), .sel(INST[14]));
  Multiplexer #(.width(8), .select(1), .enable("false")) multiplexer_81 (
    .in0(n294), .in1(n295), .out(n297), .sel(INST[14]));
  Multiplexer #(.width(8), .select(1), .enable("false")) multiplexer_82 (
    .in0(n296), .in1(n297), .out(n298), .sel(INST[15]));
  Comparator #(.width(4), .mode("unsigned")) comparator_12 (
    .a(INST[15:12]), .b(4'b0000), .gt(n300), .eq(n301), .lt(n302));
  Comparator #(.width(4), .mode("unsigned")) comparator_13 (
    .a(INST[15:12]), .b(4'b0001), .gt(n304), .eq(n305), .lt(n306));
  Comparator #(.width(4), .mode("unsigned")) comparator_14 (
    .a(INST[15:12]), .b(4'b0010), .gt(n308), .eq(n309), .lt(n310));
  Comparator #(.width(4), .mode("unsigned")) comparator_15 (
    .a(INST[15:12]), .b(4'b0011), .gt(n312), .eq(n313), .lt(n314));
  Comparator #(.width(4), .mode("unsigned")) comparator_16 (
    .a(INST[15:12]), .b(4'b0100), .gt(n316), .eq(n317), .lt(n318));
  Comparator #(.width(4), .mode("unsigned")) comparator_17 (
    .a(INST[15:12]), .b(4'b0101), .gt(n320), .eq(n321), .lt(n322));
  Comparator #(.width(4), .mode("unsigned")) comparator_18 (
    .a(INST[15:12]), .b(4'b0110), .gt(n324), .eq(n325), .lt(n326));
  Comparator #(.width(4), .mode("unsigned")) comparator_19 (
    .a(INST[15:12]), .b(4'b0111), .gt(n328), .eq(n329), .lt(n330));
  Comparator #(.width(4), .mode("unsigned")) comparator_20 (
    .a(INST[15:12]), .b(4'b1000), .gt(n332), .eq(n333), .lt(n334));
  Comparator #(.width(4), .mode("unsigned")) comparator_21 (
    .a(INST[15:12]), .b(4'b1001), .gt(n336), .eq(n337), .lt(n338));
  Comparator #(.width(4), .mode("unsigned")) comparator_22 (
    .a(INST[15:12]), .b(4'b1010), .gt(n340), .eq(n341), .lt(n342));
  Comparator #(.width(4), .mode("unsigned")) comparator_23 (
    .a(INST[15:12]), .b(4'b1011), .gt(n344), .eq(n345), .lt(n346));
  Comparator #(.width(4), .mode("unsigned")) comparator_24 (
    .a(INST[15:12]), .b(4'b1100), .gt(n348), .eq(n349), .lt(n350));
  Comparator #(.width(4), .mode("unsigned")) comparator_25 (
    .a(INST[15:12]), .b(4'b1101), .gt(n352), .eq(n353), .lt(n354));
  Comparator #(.width(4), .mode("unsigned")) comparator_26 (
    .a(INST[15:12]), .b(4'b1110), .gt(n356), .eq(n357), .lt(n358));
  Comparator #(.width(4), .mode("unsigned")) comparator_27 (
    .a(INST[15:12]), .b(4'b1111), .gt(n360), .eq(n361), .lt(n362));
  not not_10 (n363, HALTED);
  not not_11 (n364, n64);
  and and_26 (n365, n363, n364);
  or or_29 (n366, n305, n309);
  or or_30 (n367, n366, n313);
  or or_31 (n368, n367, n317);
  or or_32 (n369, n368, n321);
  or or_33 (n370, n369, n325);
  or or_34 (n371, n370, n329);
  or or_35 (n372, n371, n333);
  or or_36 (n373, n372, n337);
  or or_37 (n374, n373, n341);
  and and_27 (n375, n365, n374);
  Comparator #(.width(2), .mode("unsigned")) comparator_28 (
    .a(INST[11:10]), .b(2'b00), .gt(n376), .eq(n377), .lt(n378));
  and and_28 (n379, n375, n377);
  Multiplexer #(.width(8), .select(1), .enable("false")) multiplexer_83 (
    .in0(n298), .in1({8{1'b0}}), .out(n380), .sel(RST));
  or or_38 (n381, RST, n379);
  Register #(.width(8), .trigger("rising"), .Select("high")) register_19 (
    .D(n380), .en(n381), .Q(R0), .clk(CLK), .clr(1'b0), .cs(1'b1), .preset(1'b0));
  Comparator #(.width(2), .mode("unsigned")) comparator_29 (
    .a(INST[11:10]), .b(2'b01), .gt(n382), .eq(n383), .lt(n384));
  and and_29 (n385, n375, n383);
  Multiplexer #(.width(8), .select(1), .enable("false")) multiplexer_84 (
    .in0(n298), .in1({8{1'b0}}), .out(n386), .sel(RST));
  or or_39 (n387, RST, n385);
  Register #(.width(8), .trigger("rising"), .Select("high")) register_20 (
    .D(n386), .en(n387), .Q(R1), .clk(CLK), .clr(1'b0), .cs(1'b1), .preset(1'b0));
  Comparator #(.width(2), .mode("unsigned")) comparator_30 (
    .a(INST[11:10]), .b(2'b10), .gt(n388), .eq(n389), .lt(n390));
  and and_30 (n391, n375, n389);
  Multiplexer #(.width(8), .select(1), .enable("false")) multiplexer_85 (
    .in0(n298), .in1({8{1'b0}}), .out(n392), .sel(RST));
  or or_40 (n393, RST, n391);
  Register #(.width(8), .trigger("rising"), .Select("high")) register_21 (
    .D(n392), .en(n393), .Q(R2), .clk(CLK), .clr(1'b0), .cs(1'b1), .preset(1'b0));
  Comparator #(.width(2), .mode("unsigned")) comparator_31 (
    .a(INST[11:10]), .b(2'b11), .gt(n394), .eq(n395), .lt(n396));
  and and_31 (n397, n375, n395);
  Multiplexer #(.width(8), .select(1), .enable("false")) multiplexer_86 (
    .in0(n298), .in1({8{1'b0}}), .out(n398), .sel(RST));
  or or_41 (n399, RST, n397);
  Register #(.width(8), .trigger("rising"), .Select("high")) register_22 (
    .D(n398), .en(n399), .Q(R3), .clk(CLK), .clr(1'b0), .cs(1'b1), .preset(1'b0));
  and and_32 (n400, n365, n345);
  Comparator #(.width(4), .mode("unsigned")) comparator_32 (
    .a(INST[3:0]), .b(4'b0000), .gt(n401), .eq(n402), .lt(n403));
  and and_33 (n404, n400, n402);
  Multiplexer #(.width(8), .select(1), .enable("false")) multiplexer_87 (
    .in0(n238), .in1({8{1'b0}}), .out(n405), .sel(RST));
  or or_42 (n406, RST, n404);
  Register #(.width(8), .trigger("rising"), .Select("high")) register_23 (
    .D(n405), .en(n406), .Q(mem0), .clk(CLK), .clr(1'b0), .cs(1'b1), .preset(1'b0));
  Comparator #(.width(4), .mode("unsigned")) comparator_33 (
    .a(INST[3:0]), .b(4'b0001), .gt(n407), .eq(n408), .lt(n409));
  and and_34 (n410, n400, n408);
  Multiplexer #(.width(8), .select(1), .enable("false")) multiplexer_88 (
    .in0(n238), .in1({8{1'b0}}), .out(n411), .sel(RST));
  or or_43 (n412, RST, n410);
  Register #(.width(8), .trigger("rising"), .Select("high")) register_24 (
    .D(n411), .en(n412), .Q(mem1), .clk(CLK), .clr(1'b0), .cs(1'b1), .preset(1'b0));
  Comparator #(.width(4), .mode("unsigned")) comparator_34 (
    .a(INST[3:0]), .b(4'b0010), .gt(n413), .eq(n414), .lt(n415));
  and and_35 (n416, n400, n414);
  Multiplexer #(.width(8), .select(1), .enable("false")) multiplexer_89 (
    .in0(n238), .in1({8{1'b0}}), .out(n417), .sel(RST));
  or or_44 (n418, RST, n416);
  Register #(.width(8), .trigger("rising"), .Select("high")) register_25 (
    .D(n417), .en(n418), .Q(mem2), .clk(CLK), .clr(1'b0), .cs(1'b1), .preset(1'b0));
  Comparator #(.width(4), .mode("unsigned")) comparator_35 (
    .a(INST[3:0]), .b(4'b0011), .gt(n419), .eq(n420), .lt(n421));
  and and_36 (n422, n400, n420);
  Multiplexer #(.width(8), .select(1), .enable("false")) multiplexer_90 (
    .in0(n238), .in1({8{1'b0}}), .out(n423), .sel(RST));
  or or_45 (n424, RST, n422);
  Register #(.width(8), .trigger("rising"), .Select("high")) register_26 (
    .D(n423), .en(n424), .Q(mem3), .clk(CLK), .clr(1'b0), .cs(1'b1), .preset(1'b0));
  Comparator #(.width(4), .mode("unsigned")) comparator_36 (
    .a(INST[3:0]), .b(4'b0100), .gt(n425), .eq(n426), .lt(n427));
  and and_37 (n428, n400, n426);
  Multiplexer #(.width(8), .select(1), .enable("false")) multiplexer_91 (
    .in0(n238), .in1({8{1'b0}}), .out(n429), .sel(RST));
  or or_46 (n430, RST, n428);
  Register #(.width(8), .trigger("rising"), .Select("high")) register_27 (
    .D(n429), .en(n430), .Q(mem4), .clk(CLK), .clr(1'b0), .cs(1'b1), .preset(1'b0));
  Comparator #(.width(4), .mode("unsigned")) comparator_37 (
    .a(INST[3:0]), .b(4'b0101), .gt(n431), .eq(n432), .lt(n433));
  and and_38 (n434, n400, n432);
  Multiplexer #(.width(8), .select(1), .enable("false")) multiplexer_92 (
    .in0(n238), .in1({8{1'b0}}), .out(n435), .sel(RST));
  or or_47 (n436, RST, n434);
  Register #(.width(8), .trigger("rising"), .Select("high")) register_28 (
    .D(n435), .en(n436), .Q(mem5), .clk(CLK), .clr(1'b0), .cs(1'b1), .preset(1'b0));
  Comparator #(.width(4), .mode("unsigned")) comparator_38 (
    .a(INST[3:0]), .b(4'b0110), .gt(n437), .eq(n438), .lt(n439));
  and and_39 (n440, n400, n438);
  Multiplexer #(.width(8), .select(1), .enable("false")) multiplexer_93 (
    .in0(n238), .in1({8{1'b0}}), .out(n441), .sel(RST));
  or or_48 (n442, RST, n440);
  Register #(.width(8), .trigger("rising"), .Select("high")) register_29 (
    .D(n441), .en(n442), .Q(mem6), .clk(CLK), .clr(1'b0), .cs(1'b1), .preset(1'b0));
  Comparator #(.width(4), .mode("unsigned")) comparator_39 (
    .a(INST[3:0]), .b(4'b0111), .gt(n443), .eq(n444), .lt(n445));
  and and_40 (n446, n400, n444);
  Multiplexer #(.width(8), .select(1), .enable("false")) multiplexer_94 (
    .in0(n238), .in1({8{1'b0}}), .out(n447), .sel(RST));
  or or_49 (n448, RST, n446);
  Register #(.width(8), .trigger("rising"), .Select("high")) register_30 (
    .D(n447), .en(n448), .Q(mem7), .clk(CLK), .clr(1'b0), .cs(1'b1), .preset(1'b0));
  Comparator #(.width(4), .mode("unsigned")) comparator_40 (
    .a(INST[3:0]), .b(4'b1000), .gt(n449), .eq(n450), .lt(n451));
  and and_41 (n452, n400, n450);
  Multiplexer #(.width(8), .select(1), .enable("false")) multiplexer_95 (
    .in0(n238), .in1({8{1'b0}}), .out(n453), .sel(RST));
  or or_50 (n454, RST, n452);
  Register #(.width(8), .trigger("rising"), .Select("high")) register_31 (
    .D(n453), .en(n454), .Q(mem8), .clk(CLK), .clr(1'b0), .cs(1'b1), .preset(1'b0));
  Comparator #(.width(4), .mode("unsigned")) comparator_41 (
    .a(INST[3:0]), .b(4'b1001), .gt(n455), .eq(n456), .lt(n457));
  and and_42 (n458, n400, n456);
  Multiplexer #(.width(8), .select(1), .enable("false")) multiplexer_96 (
    .in0(n238), .in1({8{1'b0}}), .out(n459), .sel(RST));
  or or_51 (n460, RST, n458);
  Register #(.width(8), .trigger("rising"), .Select("high")) register_32 (
    .D(n459), .en(n460), .Q(mem9), .clk(CLK), .clr(1'b0), .cs(1'b1), .preset(1'b0));
  Comparator #(.width(4), .mode("unsigned")) comparator_42 (
    .a(INST[3:0]), .b(4'b1010), .gt(n461), .eq(n462), .lt(n463));
  and and_43 (n464, n400, n462);
  Multiplexer #(.width(8), .select(1), .enable("false")) multiplexer_97 (
    .in0(n238), .in1({8{1'b0}}), .out(n465), .sel(RST));
  or or_52 (n466, RST, n464);
  Register #(.width(8), .trigger("rising"), .Select("high")) register_33 (
    .D(n465), .en(n466), .Q(mem10), .clk(CLK), .clr(1'b0), .cs(1'b1), .preset(1'b0));
  Comparator #(.width(4), .mode("unsigned")) comparator_43 (
    .a(INST[3:0]), .b(4'b1011), .gt(n467), .eq(n468), .lt(n469));
  and and_44 (n470, n400, n468);
  Multiplexer #(.width(8), .select(1), .enable("false")) multiplexer_98 (
    .in0(n238), .in1({8{1'b0}}), .out(n471), .sel(RST));
  or or_53 (n472, RST, n470);
  Register #(.width(8), .trigger("rising"), .Select("high")) register_34 (
    .D(n471), .en(n472), .Q(mem11), .clk(CLK), .clr(1'b0), .cs(1'b1), .preset(1'b0));
  Comparator #(.width(4), .mode("unsigned")) comparator_44 (
    .a(INST[3:0]), .b(4'b1100), .gt(n473), .eq(n474), .lt(n475));
  and and_45 (n476, n400, n474);
  Multiplexer #(.width(8), .select(1), .enable("false")) multiplexer_99 (
    .in0(n238), .in1({8{1'b0}}), .out(n477), .sel(RST));
  or or_54 (n478, RST, n476);
  Register #(.width(8), .trigger("rising"), .Select("high")) register_35 (
    .D(n477), .en(n478), .Q(mem12), .clk(CLK), .clr(1'b0), .cs(1'b1), .preset(1'b0));
  Comparator #(.width(4), .mode("unsigned")) comparator_45 (
    .a(INST[3:0]), .b(4'b1101), .gt(n479), .eq(n480), .lt(n481));
  and and_46 (n482, n400, n480);
  Multiplexer #(.width(8), .select(1), .enable("false")) multiplexer_100 (
    .in0(n238), .in1({8{1'b0}}), .out(n483), .sel(RST));
  or or_55 (n484, RST, n482);
  Register #(.width(8), .trigger("rising"), .Select("high")) register_36 (
    .D(n483), .en(n484), .Q(mem13), .clk(CLK), .clr(1'b0), .cs(1'b1), .preset(1'b0));
  Comparator #(.width(4), .mode("unsigned")) comparator_46 (
    .a(INST[3:0]), .b(4'b1110), .gt(n485), .eq(n486), .lt(n487));
  and and_47 (n488, n400, n486);
  Multiplexer #(.width(8), .select(1), .enable("false")) multiplexer_101 (
    .in0(n238), .in1({8{1'b0}}), .out(n489), .sel(RST));
  or or_56 (n490, RST, n488);
  Register #(.width(8), .trigger("rising"), .Select("high")) register_37 (
    .D(n489), .en(n490), .Q(mem14), .clk(CLK), .clr(1'b0), .cs(1'b1), .preset(1'b0));
  Comparator #(.width(4), .mode("unsigned")) comparator_47 (
    .a(INST[3:0]), .b(4'b1111), .gt(n491), .eq(n492), .lt(n493));
  and and_48 (n494, n400, n492);
  Multiplexer #(.width(8), .select(1), .enable("false")) multiplexer_102 (
    .in0(n238), .in1({8{1'b0}}), .out(n495), .sel(RST));
  or or_57 (n496, RST, n494);
  Register #(.width(8), .trigger("rising"), .Select("high")) register_38 (
    .D(n495), .en(n496), .Q(mem15), .clk(CLK), .clr(1'b0), .cs(1'b1), .preset(1'b0));
  Comparator #(.width(8), .mode("unsigned")) comparator_48 (.a(n238), .b({8{1'b0}}), .gt(n497), .eq(n498), .lt(n499));
  and and_49 (n500, n349, n498);
  not not_12 (n501, n498);
  and and_50 (n502, n353, n501);
  or or_58 (n503, n357, n500);
  or or_59 (n504, n503, n502);
  Adder #(.width(8)) adder_4 (.a(PC), .b(8'h1), .out(n505), .cin(1'b0), .cout(n506));
  Multiplexer #(.width(8), .select(1), .enable("false")) multiplexer_103 (
    .in0(n505), .in1(INST[7:0]), .out(n507), .sel(n504));
  not not_13 (n508, n361);
  and and_51 (n509, n365, n508);
  Multiplexer #(.width(8), .select(1), .enable("false")) multiplexer_104 (
    .in0(n507), .in1(n213), .out(n510), .sel(n120));
  or or_60 (n511, n509, n120);
  and and_52 (n512, n365, n361);
  or or_61 (n513, HALTED, n512);
  Multiplexer #(.width(1), .select(1), .enable("false")) multiplexer_105 (
    .in0(n513), .in1(1'b0), .out(n514), .sel(n64));
  Multiplexer #(.width(8), .select(1), .enable("false")) multiplexer_106 (
    .in0(n510), .in1({8{1'b0}}), .out(n515), .sel(RST));
  or or_62 (n516, RST, n511);
  Register #(.width(8), .trigger("rising"), .Select("high")) register_39 (
    .D(n515), .en(n516), .Q(PC), .clk(CLK), .clr(1'b0), .cs(1'b1), .preset(1'b0));
  Multiplexer #(.width(1), .select(1), .enable("false")) multiplexer_107 (
    .in0(n514), .in1(1'b0), .out(n517), .sel(RST));
  or or_63 (n518, RST, 1'b1);
  Register #(.width(1), .trigger("rising"), .Select("high")) register_40 (
    .D(n517), .en(n518), .Q(HALTED), .clk(CLK), .clr(1'b0), .cs(1'b1), .preset(1'b0));
  Multiplexer #(.width(8), .select(1), .enable("false")) multiplexer_108 (
    .in0(mem0), .in1(mem1), .out(n523), .sel(MA[0]));
  Multiplexer #(.width(8), .select(1), .enable("false")) multiplexer_109 (
    .in0(mem2), .in1(mem3), .out(n524), .sel(MA[0]));
  Multiplexer #(.width(8), .select(1), .enable("false")) multiplexer_110 (
    .in0(mem4), .in1(mem5), .out(n525), .sel(MA[0]));
  Multiplexer #(.width(8), .select(1), .enable("false")) multiplexer_111 (
    .in0(mem6), .in1(mem7), .out(n526), .sel(MA[0]));
  Multiplexer #(.width(8), .select(1), .enable("false")) multiplexer_112 (
    .in0(mem8), .in1(mem9), .out(n527), .sel(MA[0]));
  Multiplexer #(.width(8), .select(1), .enable("false")) multiplexer_113 (
    .in0(mem10), .in1(mem11), .out(n528), .sel(MA[0]));
  Multiplexer #(.width(8), .select(1), .enable("false")) multiplexer_114 (
    .in0(mem12), .in1(mem13), .out(n529), .sel(MA[0]));
  Multiplexer #(.width(8), .select(1), .enable("false")) multiplexer_115 (
    .in0(mem14), .in1(mem15), .out(n530), .sel(MA[0]));
  Multiplexer #(.width(8), .select(1), .enable("false")) multiplexer_116 (
    .in0(n523), .in1(n524), .out(n531), .sel(MA[1]));
  Multiplexer #(.width(8), .select(1), .enable("false")) multiplexer_117 (
    .in0(n525), .in1(n526), .out(n532), .sel(MA[1]));
  Multiplexer #(.width(8), .select(1), .enable("false")) multiplexer_118 (
    .in0(n527), .in1(n528), .out(n533), .sel(MA[1]));
  Multiplexer #(.width(8), .select(1), .enable("false")) multiplexer_119 (
    .in0(n529), .in1(n530), .out(n534), .sel(MA[1]));
  Multiplexer #(.width(8), .select(1), .enable("false")) multiplexer_120 (
    .in0(n531), .in1(n532), .out(n535), .sel(MA[2]));
  Multiplexer #(.width(8), .select(1), .enable("false")) multiplexer_121 (
    .in0(n533), .in1(n534), .out(n536), .sel(MA[2]));
  Multiplexer #(.width(8), .select(1), .enable("false")) multiplexer_122 (
    .in0(n535), .in1(n536), .out(MD), .sel(MA[3]));

  // Other names for the same wires on the sheet: depth_state[1:0] = DEPTH; n173 = DEPTH[0]; n178 = DEPTH[0];
  //   n183 = DEPTH[0]; n188 = DEPTH[0]; n174 = DEPTH[1]; n179 = DEPTH[1]; n184 = DEPTH[1]; n189 = DEPTH[1];
  //   halt_state = HALTED; ie_state = IE; n5[7:0] = INST[7:0]; n9[3:0] = INST[3:0]; n105[2:0] = INST[2:0];
  //   n244 = INST[0]; n245 = INST[1]; n246 = INST[2]; n106[12:0] = INST[15:3]; n247 = INST[3]; n10[3:0] = INST[7:4];
  //   n6[1:0] = INST[9:8]; n239 = INST[8]; n240 = INST[9]; n7[1:0] = INST[11:10]; n234 = INST[10]; n235 = INST[11];
  //   n8[3:0] = INST[15:12]; n280 = INST[12]; n281 = INST[13]; n282 = INST[14]; n283 = INST[15]; n19 = IRQ[0];
  //   n20 = IRQ[1]; n21 = IRQ[2]; level_state[1:0] = LEVEL; n519 = MA[0]; n520 = MA[1]; n521 = MA[2]; n522 = MA[3];
  //   mask_state[2:0] = MASK; n25 = MASK[0]; n26 = MASK[1]; n27 = MASK[2]; n82[2:0] = {n81, n79, n77};
  //   n86[2:0] = {n55, n58, n61}; n87[2:0] = ACK; n177[7:0] = EPC; n267 = n238[0]; n275[7:1] = n238[6:0];
  //   n268 = n238[1]; n276[6:0] = n238[7:1]; n269 = n238[2]; n270 = n238[3]; n271 = n238[4]; n272 = n238[5];
  //   n273 = n238[6]; n274 = n238[7]; n537[7:0] = MD; pc_state[7:0] = PC; n22 = PENDING[0];
  //   pending_state[2:0] = PENDING; n23 = PENDING[1]; n24 = PENDING[2]; reg0[7:0] = R0; reg1[7:0] = R1;
  //   reg2[7:0] = R2; reg3[7:0] = R3
endmodule
