// Logisim project ignores-halt.circ as structural Verilog: 1 circuit, main circuit main
module main (
  input  CLK,
  input  RST,
  input  [15:0] INST,
  input  [3:0] MA,
  output [7:0] R0,
  output [7:0] R1,
  output [7:0] R2,
  output [7:0] R3,
  output [7:0] MD,
  output [7:0] PC,
  output HALTED
);

  wire n63, n66, n101, n102, n103, n105, n106, n107, n109, n110, n111, n113, n114, n115, n117, n118, n119,
       n121, n122, n123, n125, n126, n127, n129, n130, n131, n133, n134, n135, n137, n138, n139, n141, n142,
       n143, n145, n146, n147, n149, n150, n151, n153, n154, n155, n157, n158, n159, n161, n162, n163, n165,
       n166, n167, n168, n169, n170, n171, n172, n173, n174, n176, n177, n178, n179, n181, n183, n184, n185,
       n186, n188, n190, n191, n192, n193, n195, n197, n198, n199, n200, n202, n203, n204, n205, n206, n207,
       n209, n210, n211, n212, n213, n215, n216, n217, n218, n219, n221, n222, n223, n224, n225, n227, n228,
       n229, n230, n231, n233, n234, n235, n236, n237, n239, n240, n241, n242, n243, n245, n246, n247, n248,
       n249, n251, n252, n253, n254, n255, n257, n258, n259, n260, n261, n263, n264, n265, n266, n267, n269,
       n270, n271, n272, n273, n275, n276, n277, n278, n279, n281, n282, n283, n284, n285, n287, n288, n289,
       n290, n291, n293, n294, n295, n296, n297, n299, n300, n301, n302, n303, n304, n305, n306, n307, n310,
       n312, n313, n315, n316, n317, n318;
  wire [7:0] mem0, mem1, mem2, mem3, mem4, mem5, mem6, mem7, mem8, mem9, mem10, mem11, mem12, mem13, mem14,
       mem15, n35, n36, n37, n40, n41, n42, n47, n48, n49, n50, n51, n52, n53, n54, n55, n56, n57, n58, n59,
       n60, n61, n62, n65, n78, n79, n80, n85, n86, n87, n88, n89, n90, n91, n92, n93, n94, n95, n96, n97,
       n98, n99, n180, n187, n194, n201, n208, n214, n220, n226, n232, n238, n244, n250, n256, n262, n268,
       n274, n280, n286, n292, n298, n309, n311, n314, n323, n324, n325, n326, n327, n328, n329, n330, n331,
       n332, n333, n334, n335, n336;

  Multiplexer #(.width(8), .select(1), .enable("false")) multiplexer_1 (.in0(R0), .in1(R1), .out(n35), .sel(INST[10]));
  Multiplexer #(.width(8), .select(1), .enable("false")) multiplexer_2 (.in0(R2), .in1(R3), .out(n36), .sel(INST[10]));
  Multiplexer #(.width(8), .select(1), .enable("false")) multiplexer_3 (
    .in0(n35), .in1(n36), .out(n37), .sel(INST[11]));
  Multiplexer #(.width(8), .select(1), .enable("false")) multiplexer_4 (.in0(R0), .in1(R1), .out(n40), .sel(INST[8]));
  Multiplexer #(.width(8), .select(1), .enable("false")) multiplexer_5 (.in0(R2), .in1(R3), .out(n41), .sel(INST[8]));
  Multiplexer #(.width(8), .select(1), .enable("false")) multiplexer_6 (.in0(n40), .in1(n41), .out(n42), .sel(INST[9]));
  Multiplexer #(.width(8), .select(1), .enable("false")) multiplexer_7 (
    .in0(mem0), .in1(mem1), .out(n47), .sel(INST[0]));
  Multiplexer #(.width(8), .select(1), .enable("false")) multiplexer_8 (
    .in0(mem2), .in1(mem3), .out(n48), .sel(INST[0]));
  Multiplexer #(.width(8), .select(1), .enable("false")) multiplexer_9 (
    .in0(mem4), .in1(mem5), .out(n49), .sel(INST[0]));
  Multiplexer #(.width(8), .select(1), .enable("false")) multiplexer_10 (
    .in0(mem6), .in1(mem7), .out(n50), .sel(INST[0]));
  Multiplexer #(.width(8), .select(1), .enable("false")) multiplexer_11 (
    .in0(mem8), .in1(mem9), .out(n51), .sel(INST[0]));
  Multiplexer #(.width(8), .select(1), .enable("false")) multiplexer_12 (
    .in0(mem10), .in1(mem11), .out(n52), .sel(INST[0]));
  Multiplexer #(.width(8), .select(1), .enable("false")) multiplexer_13 (
    .in0(mem12), .in1(mem13), .out(n53), .sel(INST[0]));
  Multiplexer #(.width(8), .select(1), .enable("false")) multiplexer_14 (
    .in0(mem14), .in1(mem15), .out(n54), .sel(INST[0]));
  Multiplexer #(.width(8), .select(1), .enable("false")) multiplexer_15 (
    .in0(n47), .in1(n48), .out(n55), .sel(INST[1]));
  Multiplexer #(.width(8), .select(1), .enable("false")) multiplexer_16 (
    .in0(n49), .in1(n50), .out(n56), .sel(INST[1]));
  Multiplexer #(.width(8), .select(1), .enable("false")) multiplexer_17 (
    .in0(n51), .in1(n52), .out(n57), .sel(INST[1]));
  Multiplexer #(.width(8), .select(1), .enable("false")) multiplexer_18 (
    .in0(n53), .in1(n54), .out(n58), .sel(INST[1]));
  Multiplexer #(.width(8), .select(1), .enable("false")) multiplexer_19 (
    .in0(n55), .in1(n56), .out(n59), .sel(INST[2]));
  Multiplexer #(.width(8), .select(1), .enable("false")) multiplexer_20 (
    .in0(n57), .in1(n58), .out(n60), .sel(INST[2]));
  Multiplexer #(.width(8), .select(1), .enable("false")) multiplexer_21 (
    .in0(n59), .in1(n60), .out(n61), .sel(INST[3]));
  Adder #(.width(8)) adder_1 (.a(n37), .b(n42), .out(n62), .cin(1'b0), .cout(n63));
  Subtractor #(.width(8)) subtractor_1 (.a(n37), .b(n42), .out(n65), .bin(1'b0), .bout(n66));
  assign n78 = n37 ^ n42;  // XOR_Gate xor_1, 8 bits wide
  assign n79 = n37 & n42;  // AND_Gate and_1, 8 bits wide
  assign n80 = n37 | n42;  // OR_Gate or_1, 8 bits wide
  Multiplexer #(.width(8), .select(1), .enable("false")) multiplexer_22 (
    .in0({8{1'b0}}), .in1(INST[7:0]), .out(n85), .sel(INST[12]));
  Multiplexer #(.width(8), .select(1), .enable("false")) multiplexer_23 (
    .in0(n42), .in1(n62), .out(n86), .sel(INST[12]));
  Multiplexer #(.width(8), .select(1), .enable("false")) multiplexer_24 (
    .in0(n65), .in1(n78), .out(n87), .sel(INST[12]));
  Multiplexer #(.width(8), .select(1), .enable("false")) multiplexer_25 (
    .in0(n79), .in1(n80), .out(n88), .sel(INST[12]));
  Multiplexer #(.width(8), .select(1), .enable("false")) multiplexer_26 (
    .in0({n37[6:0], 1'b0}), .in1({1'b0, n37[7:1]}), .out(n89), .sel(INST[12]));
  Multiplexer #(.width(8), .select(1), .enable("false")) multiplexer_27 (
    .in0(n61), .in1({8{1'b0}}), .out(n90), .sel(INST[12]));
  Multiplexer #(.width(8), .select(1), .enable("false")) multiplexer_28 (
    .in0({8{1'b0}}), .in1({8{1'b0}}), .out(n91), .sel(INST[12]));
  Multiplexer #(.width(8), .select(1), .enable("false")) multiplexer_29 (
    .in0({8{1'b0}}), .in1({8{1'b0}}), .out(n92), .sel(INST[12]));
  Multiplexer #(.width(8), .select(1), .enable("false")) multiplexer_30 (
    .in0(n85), .in1(n86), .out(n93), .sel(INST[13]));
  Multiplexer #(.width(8), .select(1), .enable("false")) multiplexer_31 (
    .in0(n87), .in1(n88), .out(n94), .sel(INST[13]));
  Multiplexer #(.width(8), .select(1), .enable("false")) multiplexer_32 (
    .in0(n89), .in1(n90), .out(n95), .sel(INST[13]));
  Multiplexer #(.width(8), .select(1), .enable("false")) multiplexer_33 (
    .in0(n91), .in1(n92), .out(n96), .sel(INST[13]));
  Multiplexer #(.width(8), .select(1), .enable("false")) multiplexer_34 (
    .in0(n93), .in1(n94), .out(n97), .sel(INST[14]));
  Multiplexer #(.width(8), .select(1), .enable("false")) multiplexer_35 (
    .in0(n95), .in1(n96), .out(n98), .sel(INST[14]));
  Multiplexer #(.width(8), .select(1), .enable("false")) multiplexer_36 (
    .in0(n97), .in1(n98), .out(n99), .sel(INST[15]));
  Comparator #(.width(4), .mode("unsigned")) comparator_1 (
    .a(INST[15:12]), .b(4'b0000), .gt(n101), .eq(n102), .lt(n103));
  Comparator #(.width(4), .mode("unsigned")) comparator_2 (
    .a(INST[15:12]), .b(4'b0001), .gt(n105), .eq(n106), .lt(n107));
  Comparator #(.width(4), .mode("unsigned")) comparator_3 (
    .a(INST[15:12]), .b(4'b0010), .gt(n109), .eq(n110), .lt(n111));
  Comparator #(.width(4), .mode("unsigned")) comparator_4 (
    .a(INST[15:12]), .b(4'b0011), .gt(n113), .eq(n114), .lt(n115));
  Comparator #(.width(4), .mode("unsigned")) comparator_5 (
    .a(INST[15:12]), .b(4'b0100), .gt(n117), .eq(n118), .lt(n119));
  Comparator #(.width(4), .mode("unsigned")) comparator_6 (
    .a(INST[15:12]), .b(4'b0101), .gt(n121), .eq(n122), .lt(n123));
  Comparator #(.width(4), .mode("unsigned")) comparator_7 (
    .a(INST[15:12]), .b(4'b0110), .gt(n125), .eq(n126), .lt(n127));
  Comparator #(.width(4), .mode("unsigned")) comparator_8 (
    .a(INST[15:12]), .b(4'b0111), .gt(n129), .eq(n130), .lt(n131));
  Comparator #(.width(4), .mode("unsigned")) comparator_9 (
    .a(INST[15:12]), .b(4'b1000), .gt(n133), .eq(n134), .lt(n135));
  Comparator #(.width(4), .mode("unsigned")) comparator_10 (
    .a(INST[15:12]), .b(4'b1001), .gt(n137), .eq(n138), .lt(n139));
  Comparator #(.width(4), .mode("unsigned")) comparator_11 (
    .a(INST[15:12]), .b(4'b1010), .gt(n141), .eq(n142), .lt(n143));
  Comparator #(.width(4), .mode("unsigned")) comparator_12 (
    .a(INST[15:12]), .b(4'b1011), .gt(n145), .eq(n146), .lt(n147));
  Comparator #(.width(4), .mode("unsigned")) comparator_13 (
    .a(INST[15:12]), .b(4'b1100), .gt(n149), .eq(n150), .lt(n151));
  Comparator #(.width(4), .mode("unsigned")) comparator_14 (
    .a(INST[15:12]), .b(4'b1101), .gt(n153), .eq(n154), .lt(n155));
  Comparator #(.width(4), .mode("unsigned")) comparator_15 (
    .a(INST[15:12]), .b(4'b1110), .gt(n157), .eq(n158), .lt(n159));
  Comparator #(.width(4), .mode("unsigned")) comparator_16 (
    .a(INST[15:12]), .b(4'b1111), .gt(n161), .eq(n162), .lt(n163));
  or or_2 (n165, n106, n110);
  or or_3 (n166, n165, n114);
  or or_4 (n167, n166, n118);
  or or_5 (n168, n167, n122);
  or or_6 (n169, n168, n126);
  or or_7 (n170, n169, n130);
  or or_8 (n171, n170, n134);
  or or_9 (n172, n171, n138);
  or or_10 (n173, n172, n142);
  and and_2 (n174, 1'b1, n173);
  Comparator #(.width(2), .mode("unsigned")) comparator_17 (
    .a(INST[11:10]), .b(2'b00), .gt(n176), .eq(n177), .lt(n178));
  and and_3 (n179, n174, n177);
  Multiplexer #(.width(8), .select(1), .enable("false")) multiplexer_37 (
    .in0(n99), .in1({8{1'b0}}), .out(n180), .sel(RST));
  or or_11 (n181, RST, n179);
  Register #(.width(8), .trigger("rising"), .Select("high")) register_1 (
    .D(n180), .en(n181), .Q(R0), .clk(CLK), .clr(1'b0), .cs(1'b1), .preset(1'b0));
  Comparator #(.width(2), .mode("unsigned")) comparator_18 (
    .a(INST[11:10]), .b(2'b01), .gt(n183), .eq(n184), .lt(n185));
  and and_4 (n186, n174, n184);
  Multiplexer #(.width(8), .select(1), .enable("false")) multiplexer_38 (
    .in0(n99), .in1({8{1'b0}}), .out(n187), .sel(RST));
  or or_12 (n188, RST, n186);
  Register #(.width(8), .trigger("rising"), .Select("high")) register_2 (
    .D(n187), .en(n188), .Q(R1), .clk(CLK), .clr(1'b0), .cs(1'b1), .preset(1'b0));
  Comparator #(.width(2), .mode("unsigned")) comparator_19 (
    .a(INST[11:10]), .b(2'b10), .gt(n190), .eq(n191), .lt(n192));
  and and_5 (n193, n174, n191);
  Multiplexer #(.width(8), .select(1), .enable("false")) multiplexer_39 (
    .in0(n99), .in1({8{1'b0}}), .out(n194), .sel(RST));
  or or_13 (n195, RST, n193);
  Register #(.width(8), .trigger("rising"), .Select("high")) register_3 (
    .D(n194), .en(n195), .Q(R2), .clk(CLK), .clr(1'b0), .cs(1'b1), .preset(1'b0));
  Comparator #(.width(2), .mode("unsigned")) comparator_20 (
    .a(INST[11:10]), .b(2'b11), .gt(n197), .eq(n198), .lt(n199));
  and and_6 (n200, n174, n198);
  Multiplexer #(.width(8), .select(1), .enable("false")) multiplexer_40 (
    .in0(n99), .in1({8{1'b0}}), .out(n201), .sel(RST));
  or or_14 (n202, RST, n200);
  Register #(.width(8), .trigger("rising"), .Select("high")) register_4 (
    .D(n201), .en(n202), .Q(R3), .clk(CLK), .clr(1'b0), .cs(1'b1), .preset(1'b0));
  and and_7 (n203, 1'b1, n146);
  Comparator #(.width(4), .mode("unsigned")) comparator_21 (
    .a(INST[3:0]), .b(4'b0000), .gt(n204), .eq(n205), .lt(n206));
  and and_8 (n207, n203, n205);
  Multiplexer #(.width(8), .select(1), .enable("false")) multiplexer_41 (
    .in0(n37), .in1({8{1'b0}}), .out(n208), .sel(RST));
  or or_15 (n209, RST, n207);
  Register #(.width(8), .trigger("rising"), .Select("high")) register_5 (
    .D(n208), .en(n209), .Q(mem0), .clk(CLK), .clr(1'b0), .cs(1'b1), .preset(1'b0));
  Comparator #(.width(4), .mode("unsigned")) comparator_22 (
    .a(INST[3:0]), .b(4'b0001), .gt(n210), .eq(n211), .lt(n212));
  and and_9 (n213, n203, n211);
  Multiplexer #(.width(8), .select(1), .enable("false")) multiplexer_42 (
    .in0(n37), .in1({8{1'b0}}), .out(n214), .sel(RST));
  or or_16 (n215, RST, n213);
  Register #(.width(8), .trigger("rising"), .Select("high")) register_6 (
    .D(n214), .en(n215), .Q(mem1), .clk(CLK), .clr(1'b0), .cs(1'b1), .preset(1'b0));
  Comparator #(.width(4), .mode("unsigned")) comparator_23 (
    .a(INST[3:0]), .b(4'b0010), .gt(n216), .eq(n217), .lt(n218));
  and and_10 (n219, n203, n217);
  Multiplexer #(.width(8), .select(1), .enable("false")) multiplexer_43 (
    .in0(n37), .in1({8{1'b0}}), .out(n220), .sel(RST));
  or or_17 (n221, RST, n219);
  Register #(.width(8), .trigger("rising"), .Select("high")) register_7 (
    .D(n220), .en(n221), .Q(mem2), .clk(CLK), .clr(1'b0), .cs(1'b1), .preset(1'b0));
  Comparator #(.width(4), .mode("unsigned")) comparator_24 (
    .a(INST[3:0]), .b(4'b0011), .gt(n222), .eq(n223), .lt(n224));
  and and_11 (n225, n203, n223);
  Multiplexer #(.width(8), .select(1), .enable("false")) multiplexer_44 (
    .in0(n37), .in1({8{1'b0}}), .out(n226), .sel(RST));
  or or_18 (n227, RST, n225);
  Register #(.width(8), .trigger("rising"), .Select("high")) register_8 (
    .D(n226), .en(n227), .Q(mem3), .clk(CLK), .clr(1'b0), .cs(1'b1), .preset(1'b0));
  Comparator #(.width(4), .mode("unsigned")) comparator_25 (
    .a(INST[3:0]), .b(4'b0100), .gt(n228), .eq(n229), .lt(n230));
  and and_12 (n231, n203, n229);
  Multiplexer #(.width(8), .select(1), .enable("false")) multiplexer_45 (
    .in0(n37), .in1({8{1'b0}}), .out(n232), .sel(RST));
  or or_19 (n233, RST, n231);
  Register #(.width(8), .trigger("rising"), .Select("high")) register_9 (
    .D(n232), .en(n233), .Q(mem4), .clk(CLK), .clr(1'b0), .cs(1'b1), .preset(1'b0));
  Comparator #(.width(4), .mode("unsigned")) comparator_26 (
    .a(INST[3:0]), .b(4'b0101), .gt(n234), .eq(n235), .lt(n236));
  and and_13 (n237, n203, n235);
  Multiplexer #(.width(8), .select(1), .enable("false")) multiplexer_46 (
    .in0(n37), .in1({8{1'b0}}), .out(n238), .sel(RST));
  or or_20 (n239, RST, n237);
  Register #(.width(8), .trigger("rising"), .Select("high")) register_10 (
    .D(n238), .en(n239), .Q(mem5), .clk(CLK), .clr(1'b0), .cs(1'b1), .preset(1'b0));
  Comparator #(.width(4), .mode("unsigned")) comparator_27 (
    .a(INST[3:0]), .b(4'b0110), .gt(n240), .eq(n241), .lt(n242));
  and and_14 (n243, n203, n241);
  Multiplexer #(.width(8), .select(1), .enable("false")) multiplexer_47 (
    .in0(n37), .in1({8{1'b0}}), .out(n244), .sel(RST));
  or or_21 (n245, RST, n243);
  Register #(.width(8), .trigger("rising"), .Select("high")) register_11 (
    .D(n244), .en(n245), .Q(mem6), .clk(CLK), .clr(1'b0), .cs(1'b1), .preset(1'b0));
  Comparator #(.width(4), .mode("unsigned")) comparator_28 (
    .a(INST[3:0]), .b(4'b0111), .gt(n246), .eq(n247), .lt(n248));
  and and_15 (n249, n203, n247);
  Multiplexer #(.width(8), .select(1), .enable("false")) multiplexer_48 (
    .in0(n37), .in1({8{1'b0}}), .out(n250), .sel(RST));
  or or_22 (n251, RST, n249);
  Register #(.width(8), .trigger("rising"), .Select("high")) register_12 (
    .D(n250), .en(n251), .Q(mem7), .clk(CLK), .clr(1'b0), .cs(1'b1), .preset(1'b0));
  Comparator #(.width(4), .mode("unsigned")) comparator_29 (
    .a(INST[3:0]), .b(4'b1000), .gt(n252), .eq(n253), .lt(n254));
  and and_16 (n255, n203, n253);
  Multiplexer #(.width(8), .select(1), .enable("false")) multiplexer_49 (
    .in0(n37), .in1({8{1'b0}}), .out(n256), .sel(RST));
  or or_23 (n257, RST, n255);
  Register #(.width(8), .trigger("rising"), .Select("high")) register_13 (
    .D(n256), .en(n257), .Q(mem8), .clk(CLK), .clr(1'b0), .cs(1'b1), .preset(1'b0));
  Comparator #(.width(4), .mode("unsigned")) comparator_30 (
    .a(INST[3:0]), .b(4'b1001), .gt(n258), .eq(n259), .lt(n260));
  and and_17 (n261, n203, n259);
  Multiplexer #(.width(8), .select(1), .enable("false")) multiplexer_50 (
    .in0(n37), .in1({8{1'b0}}), .out(n262), .sel(RST));
  or or_24 (n263, RST, n261);
  Register #(.width(8), .trigger("rising"), .Select("high")) register_14 (
    .D(n262), .en(n263), .Q(mem9), .clk(CLK), .clr(1'b0), .cs(1'b1), .preset(1'b0));
  Comparator #(.width(4), .mode("unsigned")) comparator_31 (
    .a(INST[3:0]), .b(4'b1010), .gt(n264), .eq(n265), .lt(n266));
  and and_18 (n267, n203, n265);
  Multiplexer #(.width(8), .select(1), .enable("false")) multiplexer_51 (
    .in0(n37), .in1({8{1'b0}}), .out(n268), .sel(RST));
  or or_25 (n269, RST, n267);
  Register #(.width(8), .trigger("rising"), .Select("high")) register_15 (
    .D(n268), .en(n269), .Q(mem10), .clk(CLK), .clr(1'b0), .cs(1'b1), .preset(1'b0));
  Comparator #(.width(4), .mode("unsigned")) comparator_32 (
    .a(INST[3:0]), .b(4'b1011), .gt(n270), .eq(n271), .lt(n272));
  and and_19 (n273, n203, n271);
  Multiplexer #(.width(8), .select(1), .enable("false")) multiplexer_52 (
    .in0(n37), .in1({8{1'b0}}), .out(n274), .sel(RST));
  or or_26 (n275, RST, n273);
  Register #(.width(8), .trigger("rising"), .Select("high")) register_16 (
    .D(n274), .en(n275), .Q(mem11), .clk(CLK), .clr(1'b0), .cs(1'b1), .preset(1'b0));
  Comparator #(.width(4), .mode("unsigned")) comparator_33 (
    .a(INST[3:0]), .b(4'b1100), .gt(n276), .eq(n277), .lt(n278));
  and and_20 (n279, n203, n277);
  Multiplexer #(.width(8), .select(1), .enable("false")) multiplexer_53 (
    .in0(n37), .in1({8{1'b0}}), .out(n280), .sel(RST));
  or or_27 (n281, RST, n279);
  Register #(.width(8), .trigger("rising"), .Select("high")) register_17 (
    .D(n280), .en(n281), .Q(mem12), .clk(CLK), .clr(1'b0), .cs(1'b1), .preset(1'b0));
  Comparator #(.width(4), .mode("unsigned")) comparator_34 (
    .a(INST[3:0]), .b(4'b1101), .gt(n282), .eq(n283), .lt(n284));
  and and_21 (n285, n203, n283);
  Multiplexer #(.width(8), .select(1), .enable("false")) multiplexer_54 (
    .in0(n37), .in1({8{1'b0}}), .out(n286), .sel(RST));
  or or_28 (n287, RST, n285);
  Register #(.width(8), .trigger("rising"), .Select("high")) register_18 (
    .D(n286), .en(n287), .Q(mem13), .clk(CLK), .clr(1'b0), .cs(1'b1), .preset(1'b0));
  Comparator #(.width(4), .mode("unsigned")) comparator_35 (
    .a(INST[3:0]), .b(4'b1110), .gt(n288), .eq(n289), .lt(n290));
  and and_22 (n291, n203, n289);
  Multiplexer #(.width(8), .select(1), .enable("false")) multiplexer_55 (
    .in0(n37), .in1({8{1'b0}}), .out(n292), .sel(RST));
  or or_29 (n293, RST, n291);
  Register #(.width(8), .trigger("rising"), .Select("high")) register_19 (
    .D(n292), .en(n293), .Q(mem14), .clk(CLK), .clr(1'b0), .cs(1'b1), .preset(1'b0));
  Comparator #(.width(4), .mode("unsigned")) comparator_36 (
    .a(INST[3:0]), .b(4'b1111), .gt(n294), .eq(n295), .lt(n296));
  and and_23 (n297, n203, n295);
  Multiplexer #(.width(8), .select(1), .enable("false")) multiplexer_56 (
    .in0(n37), .in1({8{1'b0}}), .out(n298), .sel(RST));
  or or_30 (n299, RST, n297);
  Register #(.width(8), .trigger("rising"), .Select("high")) register_20 (
    .D(n298), .en(n299), .Q(mem15), .clk(CLK), .clr(1'b0), .cs(1'b1), .preset(1'b0));
  Comparator #(.width(8), .mode("unsigned")) comparator_37 (.a(n37), .b({8{1'b0}}), .gt(n300), .eq(n301), .lt(n302));
  and and_24 (n303, n150, n301);
  not not_1 (n304, n301);
  and and_25 (n305, n154, n304);
  or or_31 (n306, n158, n303);
  or or_32 (n307, n306, n305);
  Adder #(.width(8)) adder_2 (.a(PC), .b(8'h1), .out(n309), .cin(1'b0), .cout(n310));
  Multiplexer #(.width(8), .select(1), .enable("false")) multiplexer_57 (
    .in0(n309), .in1(INST[7:0]), .out(n311), .sel(n307));
  not not_2 (n312, n162);
  and and_26 (n313, 1'b1, n312);
  Multiplexer #(.width(8), .select(1), .enable("false")) multiplexer_58 (
    .in0(n311), .in1({8{1'b0}}), .out(n314), .sel(RST));
  or or_33 (n315, RST, n313);
  Register #(.width(8), .trigger("rising"), .Select("high")) register_21 (
    .D(n314), .en(n315), .Q(PC), .clk(CLK), .clr(1'b0), .cs(1'b1), .preset(1'b0));
  or or_34 (n316, HALTED, n162);
  Multiplexer #(.width(1), .select(1), .enable("false")) multiplexer_59 (.in0(n316), .in1(1'b0), .out(n317), .sel(RST));
  or or_35 (n318, RST, 1'b1);
  Register #(.width(1), .trigger("rising"), .Select("high")) register_22 (
    .D(n317), .en(n318), .Q(HALTED), .clk(CLK), .clr(1'b0), .cs(1'b1), .preset(1'b0));
  Multiplexer #(.width(8), .select(1), .enable("false")) multiplexer_60 (
    .in0(mem0), .in1(mem1), .out(n323), .sel(MA[0]));
  Multiplexer #(.width(8), .select(1), .enable("false")) multiplexer_61 (
    .in0(mem2), .in1(mem3), .out(n324), .sel(MA[0]));
  Multiplexer #(.width(8), .select(1), .enable("false")) multiplexer_62 (
    .in0(mem4), .in1(mem5), .out(n325), .sel(MA[0]));
  Multiplexer #(.width(8), .select(1), .enable("false")) multiplexer_63 (
    .in0(mem6), .in1(mem7), .out(n326), .sel(MA[0]));
  Multiplexer #(.width(8), .select(1), .enable("false")) multiplexer_64 (
    .in0(mem8), .in1(mem9), .out(n327), .sel(MA[0]));
  Multiplexer #(.width(8), .select(1), .enable("false")) multiplexer_65 (
    .in0(mem10), .in1(mem11), .out(n328), .sel(MA[0]));
  Multiplexer #(.width(8), .select(1), .enable("false")) multiplexer_66 (
    .in0(mem12), .in1(mem13), .out(n329), .sel(MA[0]));
  Multiplexer #(.width(8), .select(1), .enable("false")) multiplexer_67 (
    .in0(mem14), .in1(mem15), .out(n330), .sel(MA[0]));
  Multiplexer #(.width(8), .select(1), .enable("false")) multiplexer_68 (
    .in0(n323), .in1(n324), .out(n331), .sel(MA[1]));
  Multiplexer #(.width(8), .select(1), .enable("false")) multiplexer_69 (
    .in0(n325), .in1(n326), .out(n332), .sel(MA[1]));
  Multiplexer #(.width(8), .select(1), .enable("false")) multiplexer_70 (
    .in0(n327), .in1(n328), .out(n333), .sel(MA[1]));
  Multiplexer #(.width(8), .select(1), .enable("false")) multiplexer_71 (
    .in0(n329), .in1(n330), .out(n334), .sel(MA[1]));
  Multiplexer #(.width(8), .select(1), .enable("false")) multiplexer_72 (
    .in0(n331), .in1(n332), .out(n335), .sel(MA[2]));
  Multiplexer #(.width(8), .select(1), .enable("false")) multiplexer_73 (
    .in0(n333), .in1(n334), .out(n336), .sel(MA[2]));
  Multiplexer #(.width(8), .select(1), .enable("false")) multiplexer_74 (.in0(n335), .in1(n336), .out(MD), .sel(MA[3]));

  // Other names for the same wires on the sheet: halt_state = HALTED; n5[7:0] = INST[7:0]; n9[3:0] = INST[3:0];
  //   n43 = INST[0]; n44 = INST[1]; n45 = INST[2]; n46 = INST[3]; n10[3:0] = INST[7:4]; n6[1:0] = INST[9:8];
  //   n38 = INST[8]; n39 = INST[9]; n7[1:0] = INST[11:10]; n33 = INST[10]; n34 = INST[11]; n8[3:0] = INST[15:12];
  //   n81 = INST[12]; n82 = INST[13]; n83 = INST[14]; n84 = INST[15]; n319 = MA[0]; n320 = MA[1]; n321 = MA[2];
  //   n322 = MA[3]; n67 = n37[0]; n75[7:1] = n37[6:0]; n68 = n37[1]; n76[6:0] = n37[7:1]; n69 = n37[2]; n70 = n37[3];
  //   n71 = n37[4]; n72 = n37[5]; n73 = n37[6]; n74 = n37[7]; n337[7:0] = MD; pc_state[7:0] = PC; reg0[7:0] = R0;
  //   reg1[7:0] = R1; reg2[7:0] = R2; reg3[7:0] = R3
endmodule
