// Logisim project inverted-branches.circ as structural Verilog: 1 circuit, main circuit main
module main (
  input  CLK,
  input  RST,
  input  [15:0] INST,
  input  [3:0] MA,
  output [7:0] PC,
  output HALTED,
  output [7:0] R0,
  output [7:0] R1,
  output [7:0] R2,
  output [7:0] R3,
  output [7:0] MD
);

  wire n63, n66, n101, n102, n103, n105, n106, n107, n109, n110, n111, n113, n114, n115, n117, n118, n119,
       n121, n122, n123, n125, n126, n127, n129, n130, n131, n133, n134, n135, n137, n138, n139, n141, n142,
       n143, n145, n146, n147, n149, n150, n151, n153, n154, n155, n157, n158, n159, n161, n162, n163, n164,
       n165, n166, n167, n168, n169, n170, n171, n172, n173, n174, n176, n177, n178, n179, n182, n184, n185,
       n186, n187, n189, n191, n192, n193, n194, n196, n198, n199, n200, n201, n203, n204, n205, n206, n207,
       n208, n210, n211, n212, n213, n214, n216, n217, n218, n219, n220, n222, n223, n224, n225, n226, n228,
       n229, n230, n231, n232, n234, n235, n236, n237, n238, n240, n241, n242, n243, n244, n246, n247, n248,
       n249, n250, n252, n253, n254, n255, n256, n258, n259, n260, n261, n262, n264, n265, n266, n267, n268,
       n270, n271, n272, n273, n274, n276, n277, n278, n279, n280, n282, n283, n284, n285, n286, n288, n289,
       n290, n291, n292, n294, n295, n296, n297, n298, n300, n301, n302, n303, n304, n305, n306, n307, n308,
       n309, n312, n314, n315, n317, n318, n319, n320;
  wire [7:0] mem0, mem1, mem2, mem3, mem4, mem5, mem6, mem7, mem8, mem9, mem10, mem11, mem12, mem13, mem14,
       mem15, n35, n36, n37, n40, n41, n42, n47, n48, n49, n50, n51, n52, n53, n54, n55, n56, n57, n58, n59,
       n60, n61, n62, n65, n78, n79, n80, n85, n86, n87, n88, n89, n90, n91, n92, n93, n94, n95, n96, n97,
       n98, n99, n181, n188, n195, n202, n209, n215, n221, n227, n233, n239, n245, n251, n257, n263, n269,
       n275, n281, n287, n293, n299, n311, n313, n316, n325, n326, n327, n328, n329, n330, n331, n332, n333,
       n334, n335, n336, n337, n338;

  Multiplexer #(.width(8), .select(1), .enable("false")) multiplexer_1 (.in0(R0), .in1(R1), .out(n35), .sel(INST[10]));
  Multiplexer #(.width(8), .select(1), .enable("false")) multiplexer_2 (.in0(R2), .in1(R3), .out(n36), .sel(INST[10]));
  Multiplexer #(.width(8), .select(1), .enable("false")) multiplexer_3 (
    .in0(n35), .in1(n36), .out(n37), .sel(INST[11]));
  Multiplexer #(.width(8), .select(1), .enable("false")) multiplexer_4 (.in0(R0), .in1(R1), .out(n40), .sel(INST[8]));
  Multiplexer #(.width(8), .select(1), .enable("false")) multiplexer_5 (.in0(R2), .in1(R3), .out(n41), .sel(INST[8]));
  Multiplexer #(.width(8), .select(1), .enable("false")) multiplexer_6 (.in0(n40), .in1(n41), .out(n42), .sel(INST[9]));
  Multiplexer #(.width(8), .select(1), .enable("false")) multiplexer_7 (
    .in0(mem0), .in1(mem1), .out(n47), .sel(INST[0]));
  Multiplexer #(.width(8), .select(1), .enable("false")) multiplexer_8 (
    .in0(mem2), .in1(mem3), .out(n48), .sel(INST[0]));
  Multiplexer #(.width(8), .select(1), .enable("false")) multiplexer_9 (
    .in0(mem4), .in1(mem5), .out(n49), .sel(INST[0]));
  Multiplexer #(.width(8), .select(1), .enable("false")) multiplexer_10 (
    .in0(mem6), .in1(mem7), .out(n50), .sel(INST[0]));
  Multiplexer #(.width(8), .select(1), .enable("false")) multiplexer_11 (
    .in0(mem8), .in1(mem9), .out(n51), .sel(INST[0]));
  Multiplexer #(.width(8), .select(1), .enable("false")) multiplexer_12 (
    .in0(mem10), .in1(mem11), .out(n52), .sel(INST[0]));
  Multiplexer #(.width(8), .select(1), .enable("false")) multiplexer_13 (
    .in0(mem12), .in1(mem13), .out(n53), .sel(INST[0]));
  Multiplexer #(.width(8), .select(1), .enable("false")) multiplexer_14 (
    .in0(mem14), .in1(mem15), .out(n54), .sel(INST[0]));
  Multiplexer #(.width(8), .select(1), .enable("false")) multiplexer_15 (
    .in0(n47), .in1(n48), .out(n55), .sel(INST[1]));
  Multiplexer #(.width(8), .select(1), .enable("false")) multiplexer_16 (
    .in0(n49), .in1(n50), .out(n56), .sel(INST[1]));
  Multiplexer #(.width(8), .select(1), .enable("false")) multiplexer_17 (
    .in0(n51), .in1(n52), .out(n57), .sel(INST[1]));
  Multiplexer #(.width(8), .select(1), .enable("false")) multiplexer_18 (
    .in0(n53), .in1(n54), .out(n58), .sel(INST[1]));
  Multiplexer #(.width(8), .select(1), .enable("false")) multiplexer_19 (
    .in0(n55), .in1(n56), .out(n59), .sel(INST[2]));
  Multiplexer #(.width(8), .select(1), .enable("false")) multiplexer_20 (
    .in0(n57), .in1(n58), .out(n60), .sel(INST[2]));
  Multiplexer #(.width(8), .select(1), .enable("false")) multiplexer_21 (
    .in0(n59), .in1(n60), .out(n61), .sel(INST[3]));
  Adder #(.width(8)) adder_1 (.a(n37), .b(n42), .out(n62), .cin(1'b0), .cout(n63));
  Subtractor #(.width(8)) subtractor_1 (.a(n37), .b(n42), .out(n65), .bin(1'b0), .bout(n66));
  assign n78 = n37 ^ n42;  // XOR_Gate xor_1, 8 bits wide
  assign n79 = n37 & n42;  // AND_Gate and_1, 8 bits wide
  assign n80 = n37 | n42;  // OR_Gate or_1, 8 bits wide
  Multiplexer #(.width(8), .select(1), .enable("false")) multiplexer_22 (
    .in0({8{1'b0}}), .in1(INST[7:0]), .out(n85), .sel(INST[12]));
  Multiplexer #(.width(8), .select(1), .enable("false")) multiplexer_23 (
    .in0(n42), .in1(n62), .out(n86), .sel(INST[12]));
  Multiplexer #(.width(8), .select(1), .enable("false")) multiplexer_24 (
    .in0(n65), .in1(n78), .out(n87), .sel(INST[12]));
  Multiplexer #(.width(8), .select(1), .enable("false")) multiplexer_25 (
    .in0(n79), .in1(n80), .out(n88), .sel(INST[12]));
  Multiplexer #(.width(8), .select(1), .enable("false")) multiplexer_26 (
    .in0({n37[6:0], 1'b0}), .in1({1'b0, n37[7:1]}), .out(n89), .sel(INST[12]));
  Multiplexer #(.width(8), .select(1), .enable("false")) multiplexer_27 (
    .in0(n61), .in1({8{1'b0}}), .out(n90), .sel(INST[12]));
  Multiplexer #(.width(8), .select(1), .enable("false")) multiplexer_28 (
    .in0({8{1'b0}}), .in1({8{1'b0}}), .out(n91), .sel(INST[12]));
  Multiplexer #(.width(8), .select(1), .enable("false")) multiplexer_29 (
    .in0({8{1'b0}}), .in1({8{1'b0}}), .out(n92), .sel(INST[12]));
  Multiplexer #(.width(8), .select(1), .enable("false")) multiplexer_30 (
    .in0(n85), .in1(n86), .out(n93), .sel(INST[13]));
  Multiplexer #(.width(8), .select(1), .enable("false")) multiplexer_31 (
    .in0(n87), .in1(n88), .out(n94), .sel(INST[13]));
  Multiplexer #(.width(8), .select(1), .enable("false")) multiplexer_32 (
    .in0(n89), .in1(n90), .out(n95), .sel(INST[13]));
  Multiplexer #(.width(8), .select(1), .enable("false")) multiplexer_33 (
    .in0(n91), .in1(n92), .out(n96), .sel(INST[13]));
  Multiplexer #(.width(8), .select(1), .enable("false")) multiplexer_34 (
    .in0(n93), .in1(n94), .out(n97), .sel(INST[14]));
  Multiplexer #(.width(8), .select(1), .enable("false")) multiplexer_35 (
    .in0(n95), .in1(n96), .out(n98), .sel(INST[14]));
  Multiplexer #(.width(8), .select(1), .enable("false")) multiplexer_36 (
    .in0(n97), .in1(n98), .out(n99), .sel(INST[15]));
  Comparator #(.width(4), .mode("unsigned")) comparator_1 (
    .a(INST[15:12]), .b(4'b0000), .gt(n101), .eq(n102), .lt(n103));
  Comparator #(.width(4), .mode("unsigned")) comparator_2 (
    .a(INST[15:12]), .b(4'b0001), .gt(n105), .eq(n106), .lt(n107));
  Comparator #(.width(4), .mode("unsigned")) comparator_3 (
    .a(INST[15:12]), .b(4'b0010), .gt(n109), .eq(n110), .lt(n111));
  Comparator #(.width(4), .mode("unsigned")) comparator_4 (
    .a(INST[15:12]), .b(4'b0011), .gt(n113), .eq(n114), .lt(n115));
  Comparator #(.width(4), .mode("unsigned")) comparator_5 (
    .a(INST[15:12]), .b(4'b0100), .gt(n117), .eq(n118), .lt(n119));
  Comparator #(.width(4), .mode("unsigned")) comparator_6 (
    .a(INST[15:12]), .b(4'b0101), .gt(n121), .eq(n122), .lt(n123));
  Comparator #(.width(4), .mode("unsigned")) comparator_7 (
    .a(INST[15:12]), .b(4'b0110), .gt(n125), .eq(n126), .lt(n127));
  Comparator #(.width(4), .mode("unsigned")) comparator_8 (
    .a(INST[15:12]), .b(4'b0111), .gt(n129), .eq(n130), .lt(n131));
  Comparator #(.width(4), .mode("unsigned")) comparator_9 (
    .a(INST[15:12]), .b(4'b1000), .gt(n133), .eq(n134), .lt(n135));
  Comparator #(.width(4), .mode("unsigned")) comparator_10 (
    .a(INST[15:12]), .b(4'b1001), .gt(n137), .eq(n138), .lt(n139));
  Comparator #(.width(4), .mode("unsigned")) comparator_11 (
    .a(INST[15:12]), .b(4'b1010), .gt(n141), .eq(n142), .lt(n143));
  Comparator #(.width(4), .mode("unsigned")) comparator_12 (
    .a(INST[15:12]), .b(4'b1011), .gt(n145), .eq(n146), .lt(n147));
  Comparator #(.width(4), .mode("unsigned")) comparator_13 (
    .a(INST[15:12]), .b(4'b1100), .gt(n149), .eq(n150), .lt(n151));
  Comparator #(.width(4), .mode("unsigned")) comparator_14 (
    .a(INST[15:12]), .b(4'b1101), .gt(n153), .eq(n154), .lt(n155));
  Comparator #(.width(4), .mode("unsigned")) comparator_15 (
    .a(INST[15:12]), .b(4'b1110), .gt(n157), .eq(n158), .lt(n159));
  Comparator #(.width(4), .mode("unsigned")) comparator_16 (
    .a(INST[15:12]), .b(4'b1111), .gt(n161), .eq(n162), .lt(n163));
  not not_1 (n164, HALTED);
  or or_2 (n165, n106, n110);
  or or_3 (n166, n165, n114);
  or or_4 (n167, n166, n118);
  or or_5 (n168, n167, n122);
  or or_6 (n169, n168, n126);
  or or_7 (n170, n169, n130);
  or or_8 (n171, n170, n134);
  or or_9 (n172, n171, n138);
  or or_10 (n173, n172, n142);
  and and_2 (n174, n164, n173);
  Comparator #(.width(2), .mode("unsigned")) comparator_17 (
    .a(INST[11:10]), .b(2'b00), .gt(n176), .eq(n177), .lt(n178));
  and and_3 (n179, n174, n177);
  Multiplexer #(.width(8), .select(1), .enable("false")) multiplexer_37 (
    .in0(n99), .in1({8{1'b0}}), .out(n181), .sel(RST));
  or or_11 (n182, RST, n179);
  Register #(.width(8), .trigger("rising"), .Select("high")) register_1 (
    .D(n181), .en(n182), .Q(R0), .clk(CLK), .clr(1'b0), .cs(1'b1), .preset(1'b0));
  Comparator #(.width(2), .mode("unsigned")) comparator_18 (
    .a(INST[11:10]), .b(2'b01), .gt(n184), .eq(n185), .lt(n186));
  and and_4 (n187, n174, n185);
  Multiplexer #(.width(8), .select(1), .enable("false")) multiplexer_38 (
    .in0(n99), .in1({8{1'b0}}), .out(n188), .sel(RST));
  or or_12 (n189, RST, n187);
  Register #(.width(8), .trigger("rising"), .Select("high")) register_2 (
    .D(n188), .en(n189), .Q(R1), .clk(CLK), .clr(1'b0), .cs(1'b1), .preset(1'b0));
  Comparator #(.width(2), .mode("unsigned")) comparator_19 (
    .a(INST[11:10]), .b(2'b10), .gt(n191), .eq(n192), .lt(n193));
  and and_5 (n194, n174, n192);
  Multiplexer #(.width(8), .select(1), .enable("false")) multiplexer_39 (
    .in0(n99), .in1({8{1'b0}}), .out(n195), .sel(RST));
  or or_13 (n196, RST, n194);
  Register #(.width(8), .trigger("rising"), .Select("high")) register_3 (
    .D(n195), .en(n196), .Q(R2), .clk(CLK), .clr(1'b0), .cs(1'b1), .preset(1'b0));
  Comparator #(.width(2), .mode("unsigned")) comparator_20 (
    .a(INST[11:10]), .b(2'b11), .gt(n198), .eq(n199), .lt(n200));
  and and_6 (n201, n174, n199);
  Multiplexer #(.width(8), .select(1), .enable("false")) multiplexer_40 (
    .in0(n99), .in1({8{1'b0}}), .out(n202), .sel(RST));
  or or_14 (n203, RST, n201);
  Register #(.width(8), .trigger("rising"), .Select("high")) register_4 (
    .D(n202), .en(n203), .Q(R3), .clk(CLK), .clr(1'b0), .cs(1'b1), .preset(1'b0));
  and and_7 (n204, n164, n146);
  Comparator #(.width(4), .mode("unsigned")) comparator_21 (
    .a(INST[3:0]), .b(4'b0000), .gt(n205), .eq(n206), .lt(n207));
  and and_8 (n208, n204, n206);
  Multiplexer #(.width(8), .select(1), .enable("false")) multiplexer_41 (
    .in0(n37), .in1({8{1'b0}}), .out(n209), .sel(RST));
  or or_15 (n210, RST, n208);
  Register #(.width(8), .trigger("rising"), .Select("high")) register_5 (
    .D(n209), .en(n210), .Q(mem0), .clk(CLK), .clr(1'b0), .cs(1'b1), .preset(1'b0));
  Comparator #(.width(4), .mode("unsigned")) comparator_22 (
    .a(INST[3:0]), .b(4'b0001), .gt(n211), .eq(n212), .lt(n213));
  and and_9 (n214, n204, n212);
  Multiplexer #(.width(8), .select(1), .enable("false")) multiplexer_42 (
    .in0(n37), .in1({8{1'b0}}), .out(n215), .sel(RST));
  or or_16 (n216, RST, n214);
  Register #(.width(8), .trigger("rising"), .Select("high")) register_6 (
    .D(n215), .en(n216), .Q(mem1), .clk(CLK), .clr(1'b0), .cs(1'b1), .preset(1'b0));
  Comparator #(.width(4), .mode("unsigned")) comparator_23 (
    .a(INST[3:0]), .b(4'b0010), .gt(n217), .eq(n218), .lt(n219));
  and and_10 (n220, n204, n218);
  Multiplexer #(.width(8), .select(1), .enable("false")) multiplexer_43 (
    .in0(n37), .in1({8{1'b0}}), .out(n221), .sel(RST));
  or or_17 (n222, RST, n220);
  Register #(.width(8), .trigger("rising"), .Select("high")) register_7 (
    .D(n221), .en(n222), .Q(mem2), .clk(CLK), .clr(1'b0), .cs(1'b1), .preset(1'b0));
  Comparator #(.width(4), .mode("unsigned")) comparator_24 (
    .a(INST[3:0]), .b(4'b0011), .gt(n223), .eq(n224), .lt(n225));
  and and_11 (n226, n204, n224);
  Multiplexer #(.width(8), .select(1), .enable("false")) multiplexer_44 (
    .in0(n37), .in1({8{1'b0}}), .out(n227), .sel(RST));
  or or_18 (n228, RST, n226);
  Register #(.width(8), .trigger("rising"), .Select("high")) register_8 (
    .D(n227), .en(n228), .Q(mem3), .clk(CLK), .clr(1'b0), .cs(1'b1), .preset(1'b0));
  Comparator #(.width(4), .mode("unsigned")) comparator_25 (
    .a(INST[3:0]), .b(4'b0100), .gt(n229), .eq(n230), .lt(n231));
  and and_12 (n232, n204, n230);
  Multiplexer #(.width(8), .select(1), .enable("false")) multiplexer_45 (
    .in0(n37), .in1({8{1'b0}}), .out(n233), .sel(RST));
  or or_19 (n234, RST, n232);
  Register #(.width(8), .trigger("rising"), .Select("high")) register_9 (
    .D(n233), .en(n234), .Q(mem4), .clk(CLK), .clr(1'b0), .cs(1'b1), .preset(1'b0));
  Comparator #(.width(4), .mode("unsigned")) comparator_26 (
    .a(INST[3:0]), .b(4'b0101), .gt(n235), .eq(n236), .lt(n237));
  and and_13 (n238, n204, n236);
  Multiplexer #(.width(8), .select(1), .enable("false")) multiplexer_46 (
    .in0(n37), .in1({8{1'b0}}), .out(n239), .sel(RST));
  or or_20 (n240, RST, n238);
  Register #(.width(8), .trigger("rising"), .Select("high")) register_10 (
    .D(n239), .en(n240), .Q(mem5), .clk(CLK), .clr(1'b0), .cs(1'b1), .preset(1'b0));
  Comparator #(.width(4), .mode("unsigned")) comparator_27 (
    .a(INST[3:0]), .b(4'b0110), .gt(n241), .eq(n242), .lt(n243));
  and and_14 (n244, n204, n242);
  Multiplexer #(.width(8), .select(1), .enable("false")) multiplexer_47 (
    .in0(n37), .in1({8{1'b0}}), .out(n245), .sel(RST));
  or or_21 (n246, RST, n244);
  Register #(.width(8), .trigger("rising"), .Select("high")) register_11 (
    .D(n245), .en(n246), .Q(mem6), .clk(CLK), .clr(1'b0), .cs(1'b1), .preset(1'b0));
  Comparator #(.width(4), .mode("unsigned")) comparator_28 (
    .a(INST[3:0]), .b(4'b0111), .gt(n247), .eq(n248), .lt(n249));
  and and_15 (n250, n204, n248);
  Multiplexer #(.width(8), .select(1), .enable("false")) multiplexer_48 (
    .in0(n37), .in1({8{1'b0}}), .out(n251), .sel(RST));
  or or_22 (n252, RST, n250);
  Register #(.width(8), .trigger("rising"), .Select("high")) register_12 (
    .D(n251), .en(n252), .Q(mem7), .clk(CLK), .clr(1'b0), .cs(1'b1), .preset(1'b0));
  Comparator #(.width(4), .mode("unsigned")) comparator_29 (
    .a(INST[3:0]), .b(4'b1000), .gt(n253), .eq(n254), .lt(n255));
  and and_16 (n256, n204, n254);
  Multiplexer #(.width(8), .select(1), .enable("false")) multiplexer_49 (
    .in0(n37), .in1({8{1'b0}}), .out(n257), .sel(RST));
  or or_23 (n258, RST, n256);
  Register #(.width(8), .trigger("rising"), .Select("high")) register_13 (
    .D(n257), .en(n258), .Q(mem8), .clk(CLK), .clr(1'b0), .cs(1'b1), .preset(1'b0));
  Comparator #(.width(4), .mode("unsigned")) comparator_30 (
    .a(INST[3:0]), .b(4'b1001), .gt(n259), .eq(n260), .lt(n261));
  and and_17 (n262, n204, n260);
  Multiplexer #(.width(8), .select(1), .enable("false")) multiplexer_50 (
    .in0(n37), .in1({8{1'b0}}), .out(n263), .sel(RST));
  or or_24 (n264, RST, n262);
  Register #(.width(8), .trigger("rising"), .Select("high")) register_14 (
    .D(n263), .en(n264), .Q(mem9), .clk(CLK), .clr(1'b0), .cs(1'b1), .preset(1'b0));
  Comparator #(.width(4), .mode("unsigned")) comparator_31 (
    .a(INST[3:0]), .b(4'b1010), .gt(n265), .eq(n266), .lt(n267));
  and and_18 (n268, n204, n266);
  Multiplexer #(.width(8), .select(1), .enable("false")) multiplexer_51 (
    .in0(n37), .in1({8{1'b0}}), .out(n269), .sel(RST));
  or or_25 (n270, RST, n268);
  Register #(.width(8), .trigger("rising"), .Select("high")) register_15 (
    .D(n269), .en(n270), .Q(mem10), .clk(CLK), .clr(1'b0), .cs(1'b1), .preset(1'b0));
  Comparator #(.width(4), .mode("unsigned")) comparator_32 (
    .a(INST[3:0]), .b(4'b1011), .gt(n271), .eq(n272), .lt(n273));
  and and_19 (n274, n204, n272);
  Multiplexer #(.width(8), .select(1), .enable("false")) multiplexer_52 (
    .in0(n37), .in1({8{1'b0}}), .out(n275), .sel(RST));
  or or_26 (n276, RST, n274);
  Register #(.width(8), .trigger("rising"), .Select("high")) register_16 (
    .D(n275), .en(n276), .Q(mem11), .clk(CLK), .clr(1'b0), .cs(1'b1), .preset(1'b0));
  Comparator #(.width(4), .mode("unsigned")) comparator_33 (
    .a(INST[3:0]), .b(4'b1100), .gt(n277), .eq(n278), .lt(n279));
  and and_20 (n280, n204, n278);
  Multiplexer #(.width(8), .select(1), .enable("false")) multiplexer_53 (
    .in0(n37), .in1({8{1'b0}}), .out(n281), .sel(RST));
  or or_27 (n282, RST, n280);
  Register #(.width(8), .trigger("rising"), .Select("high")) register_17 (
    .D(n281), .en(n282), .Q(mem12), .clk(CLK), .clr(1'b0), .cs(1'b1), .preset(1'b0));
  Comparator #(.width(4), .mode("unsigned")) comparator_34 (
    .a(INST[3:0]), .b(4'b1101), .gt(n283), .eq(n284), .lt(n285));
  and and_21 (n286, n204, n284);
  Multiplexer #(.width(8), .select(1), .enable("false")) multiplexer_54 (
    .in0(n37), .in1({8{1'b0}}), .out(n287), .sel(RST));
  or or_28 (n288, RST, n286);
  Register #(.width(8), .trigger("rising"), .Select("high")) register_18 (
    .D(n287), .en(n288), .Q(mem13), .clk(CLK), .clr(1'b0), .cs(1'b1), .preset(1'b0));
  Comparator #(.width(4), .mode("unsigned")) comparator_35 (
    .a(INST[3:0]), .b(4'b1110), .gt(n289), .eq(n290), .lt(n291));
  and and_22 (n292, n204, n290);
  Multiplexer #(.width(8), .select(1), .enable("false")) multiplexer_55 (
    .in0(n37), .in1({8{1'b0}}), .out(n293), .sel(RST));
  or or_29 (n294, RST, n292);
  Register #(.width(8), .trigger("rising"), .Select("high")) register_19 (
    .D(n293), .en(n294), .Q(mem14), .clk(CLK), .clr(1'b0), .cs(1'b1), .preset(1'b0));
  Comparator #(.width(4), .mode("unsigned")) comparator_36 (
    .a(INST[3:0]), .b(4'b1111), .gt(n295), .eq(n296), .lt(n297));
  and and_23 (n298, n204, n296);
  Multiplexer #(.width(8), .select(1), .enable("false")) multiplexer_56 (
    .in0(n37), .in1({8{1'b0}}), .out(n299), .sel(RST));
  or or_30 (n300, RST, n298);
  Register #(.width(8), .trigger("rising"), .Select("high")) register_20 (
    .D(n299), .en(n300), .Q(mem15), .clk(CLK), .clr(1'b0), .cs(1'b1), .preset(1'b0));
  Comparator #(.width(8), .mode("unsigned")) comparator_37 (.a(n37), .b({8{1'b0}}), .gt(n301), .eq(n302), .lt(n303));
  not not_2 (n304, n302);
  and and_24 (n305, n150, n304);
  not not_3 (n306, n304);
  and and_25 (n307, n154, n306);
  or or_31 (n308, n158, n305);
  or or_32 (n309, n308, n307);
  Adder #(.width(8)) adder_2 (.a(PC), .b(8'h1), .out(n311), .cin(1'b0), .cout(n312));
  Multiplexer #(.width(8), .select(1), .enable("false")) multiplexer_57 (
    .in0(n311), .in1(INST[7:0]), .out(n313), .sel(n309));
  not not_4 (n314, n162);
  and and_26 (n315, n164, n314);
  Multiplexer #(.width(8), .select(1), .enable("false")) multiplexer_58 (
    .in0(n313), .in1({8{1'b0}}), .out(n316), .sel(RST));
  or or_33 (n317, RST, n315);
  Register #(.width(8), .trigger("rising"), .Select("high")) register_21 (
    .D(n316), .en(n317), .Q(PC), .clk(CLK), .clr(1'b0), .cs(1'b1), .preset(1'b0));
  or or_34 (n318, HALTED, n162);
  Multiplexer #(.width(1), .select(1), .enable("false")) multiplexer_59 (.in0(n318), .in1(1'b0), .out(n319), .sel(RST));
  or or_35 (n320, RST, 1'b1);
  Register #(.width(1), .trigger("rising"), .Select("high")) register_22 (
    .D(n319), .en(n320), .Q(HALTED), .clk(CLK), .clr(1'b0), .cs(1'b1), .preset(1'b0));
  Multiplexer #(.width(8), .select(1), .enable("false")) multiplexer_60 (
    .in0(mem0), .in1(mem1), .out(n325), .sel(MA[0]));
  Multiplexer #(.width(8), .select(1), .enable("false")) multiplexer_61 (
    .in0(mem2), .in1(mem3), .out(n326), .sel(MA[0]));
  Multiplexer #(.width(8), .select(1), .enable("false")) multiplexer_62 (
    .in0(mem4), .in1(mem5), .out(n327), .sel(MA[0]));
  Multiplexer #(.width(8), .select(1), .enable("false")) multiplexer_63 (
    .in0(mem6), .in1(mem7), .out(n328), .sel(MA[0]));
  Multiplexer #(.width(8), .select(1), .enable("false")) multiplexer_64 (
    .in0(mem8), .in1(mem9), .out(n329), .sel(MA[0]));
  Multiplexer #(.width(8), .select(1), .enable("false")) multiplexer_65 (
    .in0(mem10), .in1(mem11), .out(n330), .sel(MA[0]));
  Multiplexer #(.width(8), .select(1), .enable("false")) multiplexer_66 (
    .in0(mem12), .in1(mem13), .out(n331), .sel(MA[0]));
  Multiplexer #(.width(8), .select(1), .enable("false")) multiplexer_67 (
    .in0(mem14), .in1(mem15), .out(n332), .sel(MA[0]));
  Multiplexer #(.width(8), .select(1), .enable("false")) multiplexer_68 (
    .in0(n325), .in1(n326), .out(n333), .sel(MA[1]));
  Multiplexer #(.width(8), .select(1), .enable("false")) multiplexer_69 (
    .in0(n327), .in1(n328), .out(n334), .sel(MA[1]));
  Multiplexer #(.width(8), .select(1), .enable("false")) multiplexer_70 (
    .in0(n329), .in1(n330), .out(n335), .sel(MA[1]));
  Multiplexer #(.width(8), .select(1), .enable("false")) multiplexer_71 (
    .in0(n331), .in1(n332), .out(n336), .sel(MA[1]));
  Multiplexer #(.width(8), .select(1), .enable("false")) multiplexer_72 (
    .in0(n333), .in1(n334), .out(n337), .sel(MA[2]));
  Multiplexer #(.width(8), .select(1), .enable("false")) multiplexer_73 (
    .in0(n335), .in1(n336), .out(n338), .sel(MA[2]));
  Multiplexer #(.width(8), .select(1), .enable("false")) multiplexer_74 (.in0(n337), .in1(n338), .out(MD), .sel(MA[3]));

  // Other names for the same wires on the sheet: halt_state = HALTED; n5[7:0] = INST[7:0]; n9[3:0] = INST[3:0];
  //   n43 = INST[0]; n44 = INST[1]; n45 = INST[2]; n46 = INST[3]; n10[3:0] = INST[7:4]; n6[1:0] = INST[9:8];
  //   n38 = INST[8]; n39 = INST[9]; n7[1:0] = INST[11:10]; n33 = INST[10]; n34 = INST[11]; n8[3:0] = INST[15:12];
  //   n81 = INST[12]; n82 = INST[13]; n83 = INST[14]; n84 = INST[15]; n321 = MA[0]; n322 = MA[1]; n323 = MA[2];
  //   n324 = MA[3]; n67 = n37[0]; n75[7:1] = n37[6:0]; n68 = n37[1]; n76[6:0] = n37[7:1]; n69 = n37[2]; n70 = n37[3];
  //   n71 = n37[4]; n72 = n37[5]; n73 = n37[6]; n74 = n37[7]; n339[7:0] = MD; pc_state[7:0] = PC; reg0[7:0] = R0;
  //   reg1[7:0] = R1; reg2[7:0] = R2; reg3[7:0] = R3
endmodule
