// Logisim project reference.circ as structural Verilog: 1 circuit, main circuit main
module main (
  input  A,
  input  B,
  input  Cin,
  output Sum,
  output Cout
);

  wire AB, AxB, AxBC;

  xor xor_1 (AxB, A, B);
  and and_1 (AB, A, B);
  xor xor_2 (Sum, AxB, Cin);
  and and_2 (AxBC, AxB, Cin);
  or or_1 (Cout, AB, AxBC);
endmodule
