// Logisim project async-reset.circ as structural Verilog: 1 circuit, main circuit main
module main (
  input  CLK,
  input  RST,
  input  WE,
  input  [2:0] WA,
  input  [7:0] WD,
  input  [2:0] RA,
  input  [2:0] RB,
  output [7:0] QA,
  output [7:0] QB
);

  wire n9, n10, n11, n12, n17, n18, n19, n20, n23, n24, n25, n26, n29, n30, n31, n32, n35, n36, n37, n38,
       n41, n42, n43, n44, n47, n48, n49, n50, n53, n54, n55, n56;
  wire [7:0] n15, n21, n27, n33, n39, n45, n51, n57, n61, n62, n63, n64, n65, n66, n71, n72, n73, n74, n75,
       n76;

  Comparator #(.width(3), .mode("unsigned")) comparator_1 (.a(WA), .b(3'b000), .gt(n9), .eq(n10), .lt(n11));
  and and_1 (n12, WE, n10);
  Register #(.width(8), .trigger("rising"), .Select("high")) register_1 (
    .D(WD), .en(n12), .Q(n15), .clk(CLK), .clr(RST), .cs(1'b1), .preset(1'b0));
  Comparator #(.width(3), .mode("unsigned")) comparator_2 (.a(WA), .b(3'b001), .gt(n17), .eq(n18), .lt(n19));
  and and_2 (n20, WE, n18);
  Register #(.width(8), .trigger("rising"), .Select("high")) register_2 (
    .D(WD), .en(n20), .Q(n21), .clk(CLK), .clr(RST), .cs(1'b1), .preset(1'b0));
  Comparator #(.width(3), .mode("unsigned")) comparator_3 (.a(WA), .b(3'b010), .gt(n23), .eq(n24), .lt(n25));
  and and_3 (n26, WE, n24);
  Register #(.width(8), .trigger("rising"), .Select("high")) register_3 (
    .D(WD), .en(n26), .Q(n27), .clk(CLK), .clr(RST), .cs(1'b1), .preset(1'b0));
  Comparator #(.width(3), .mode("unsigned")) comparator_4 (.a(WA), .b(3'b011), .gt(n29), .eq(n30), .lt(n31));
  and and_4 (n32, WE, n30);
  Register #(.width(8), .trigger("rising"), .Select("high")) register_4 (
    .D(WD), .en(n32), .Q(n33), .clk(CLK), .clr(RST), .cs(1'b1), .preset(1'b0));
  Comparator #(.width(3), .mode("unsigned")) comparator_5 (.a(WA), .b(3'b100), .gt(n35), .eq(n36), .lt(n37));
  and and_5 (n38, WE, n36);
  Register #(.width(8), .trigger("rising"), .Select("high")) register_5 (
    .D(WD), .en(n38), .Q(n39), .clk(CLK), .clr(RST), .cs(1'b1), .preset(1'b0));
  Comparator #(.width(3), .mode("unsigned")) comparator_6 (.a(WA), .b(3'b101), .gt(n41), .eq(n42), .lt(n43));
  and and_6 (n44, WE, n42);
  Register #(.width(8), .trigger("rising"), .Select("high")) register_6 (
    .D(WD), .en(n44), .Q(n45), .clk(CLK), .clr(RST), .cs(1'b1), .preset(1'b0));
  Comparator #(.width(3), .mode("unsigned")) comparator_7 (.a(WA), .b(3'b110), .gt(n47), .eq(n48), .lt(n49));
  and and_7 (n50, WE, n48);
  Register #(.width(8), .trigger("rising"), .Select("high")) register_7 (
    .D(WD), .en(n50), .Q(n51), .clk(CLK), .clr(RST), .cs(1'b1), .preset(1'b0));
  Comparator #(.width(3), .mode("unsigned")) comparator_8 (.a(WA), .b(3'b111), .gt(n53), .eq(n54), .lt(n55));
  and and_8 (n56, WE, n54);
  Register #(.width(8), .trigger("rising"), .Select("high")) register_8 (
    .D(WD), .en(n56), .Q(n57), .clk(CLK), .clr(RST), .cs(1'b1), .preset(1'b0));
  Multiplexer #(.width(8), .select(1), .enable("false")) multiplexer_1 (.in0(n15), .in1(n21), .out(n61), .sel(RA[0]));
  Multiplexer #(.width(8), .select(1), .enable("false")) multiplexer_2 (.in0(n27), .in1(n33), .out(n62), .sel(RA[0]));
  Multiplexer #(.width(8), .select(1), .enable("false")) multiplexer_3 (.in0(n39), .in1(n45), .out(n63), .sel(RA[0]));
  Multiplexer #(.width(8), .select(1), .enable("false")) multiplexer_4 (.in0(n51), .in1(n57), .out(n64), .sel(RA[0]));
  Multiplexer #(.width(8), .select(1), .enable("false")) multiplexer_5 (.in0(n61), .in1(n62), .out(n65), .sel(RA[1]));
  Multiplexer #(.width(8), .select(1), .enable("false")) multiplexer_6 (.in0(n63), .in1(n64), .out(n66), .sel(RA[1]));
  Multiplexer #(.width(8), .select(1), .enable("false")) multiplexer_7 (.in0(n65), .in1(n66), .out(QA), .sel(RA[2]));
  Multiplexer #(.width(8), .select(1), .enable("false")) multiplexer_8 (.in0(n15), .in1(n21), .out(n71), .sel(RB[0]));
  Multiplexer #(.width(8), .select(1), .enable("false")) multiplexer_9 (.in0(n27), .in1(n33), .out(n72), .sel(RB[0]));
  Multiplexer #(.width(8), .select(1), .enable("false")) multiplexer_10 (.in0(n39), .in1(n45), .out(n73), .sel(RB[0]));
  Multiplexer #(.width(8), .select(1), .enable("false")) multiplexer_11 (.in0(n51), .in1(n57), .out(n74), .sel(RB[0]));
  Multiplexer #(.width(8), .select(1), .enable("false")) multiplexer_12 (.in0(n71), .in1(n72), .out(n75), .sel(RB[1]));
  Multiplexer #(.width(8), .select(1), .enable("false")) multiplexer_13 (.in0(n73), .in1(n74), .out(n76), .sel(RB[1]));
  Multiplexer #(.width(8), .select(1), .enable("false")) multiplexer_14 (.in0(n75), .in1(n76), .out(QB), .sel(RB[2]));

  // Other names for the same wires on the sheet: n67[7:0] = QA; n77[7:0] = QB; n58 = RA[0]; n59 = RA[1]; n60 = RA[2];
  //   n68 = RB[0]; n69 = RB[1]; n70 = RB[2]
endmodule
