// Logisim project falling-edge.circ as structural Verilog: 1 circuit, main circuit main
module main (
  input  CLK,
  input  RST,
  input  WE,
  input  [2:0] WA,
  input  [7:0] WD,
  input  [2:0] RA,
  input  [2:0] RB,
  output [7:0] QB,
  output [7:0] QA
);

  wire n9, n10, n11, n12, n18, n20, n21, n22, n23, n26, n28, n29, n30, n31, n34, n36, n37, n38, n39, n42,
       n44, n45, n46, n47, n50, n52, n53, n54, n55, n58, n60, n61, n62, n63, n66, n68, n69, n70, n71, n74;
  wire [7:0] n15, n17, n24, n25, n32, n33, n40, n41, n48, n49, n56, n57, n64, n65, n72, n73, n78, n79, n80,
       n81, n82, n83, n88, n89, n90, n91, n92, n93;

  Comparator #(.width(3), .mode("unsigned")) comparator_1 (.a(WA), .b(3'b000), .gt(n9), .eq(n10), .lt(n11));
  and and_1 (n12, WE, n10);
  Multiplexer #(.width(8), .select(1), .enable("false")) multiplexer_1 (
    .in0(WD), .in1({8{1'b0}}), .out(n17), .sel(RST));
  or or_1 (n18, RST, n12);
  Register #(.width(8), .trigger("falling"), .Select("high")) register_1 (
    .D(n17), .en(n18), .Q(n15), .clk(CLK), .clr(1'b0), .cs(1'b1), .preset(1'b0));
  Comparator #(.width(3), .mode("unsigned")) comparator_2 (.a(WA), .b(3'b001), .gt(n20), .eq(n21), .lt(n22));
  and and_2 (n23, WE, n21);
  Multiplexer #(.width(8), .select(1), .enable("false")) multiplexer_2 (
    .in0(WD), .in1({8{1'b0}}), .out(n25), .sel(RST));
  or or_2 (n26, RST, n23);
  Register #(.width(8), .trigger("falling"), .Select("high")) register_2 (
    .D(n25), .en(n26), .Q(n24), .clk(CLK), .clr(1'b0), .cs(1'b1), .preset(1'b0));
  Comparator #(.width(3), .mode("unsigned")) comparator_3 (.a(WA), .b(3'b010), .gt(n28), .eq(n29), .lt(n30));
  and and_3 (n31, WE, n29);
  Multiplexer #(.width(8), .select(1), .enable("false")) multiplexer_3 (
    .in0(WD), .in1({8{1'b0}}), .out(n33), .sel(RST));
  or or_3 (n34, RST, n31);
  Register #(.width(8), .trigger("falling"), .Select("high")) register_3 (
    .D(n33), .en(n34), .Q(n32), .clk(CLK), .clr(1'b0), .cs(1'b1), .preset(1'b0));
  Comparator #(.width(3), .mode("unsigned")) comparator_4 (.a(WA), .b(3'b011), .gt(n36), .eq(n37), .lt(n38));
  and and_4 (n39, WE, n37);
  Multiplexer #(.width(8), .select(1), .enable("false")) multiplexer_4 (
    .in0(WD), .in1({8{1'b0}}), .out(n41), .sel(RST));
  or or_4 (n42, RST, n39);
  Register #(.width(8), .trigger("falling"), .Select("high")) register_4 (
    .D(n41), .en(n42), .Q(n40), .clk(CLK), .clr(1'b0), .cs(1'b1), .preset(1'b0));
  Comparator #(.width(3), .mode("unsigned")) comparator_5 (.a(WA), .b(3'b100), .gt(n44), .eq(n45), .lt(n46));
  and and_5 (n47, WE, n45);
  Multiplexer #(.width(8), .select(1), .enable("false")) multiplexer_5 (
    .in0(WD), .in1({8{1'b0}}), .out(n49), .sel(RST));
  or or_5 (n50, RST, n47);
  Register #(.width(8), .trigger("falling"), .Select("high")) register_5 (
    .D(n49), .en(n50), .Q(n48), .clk(CLK), .clr(1'b0), .cs(1'b1), .preset(1'b0));
  Comparator #(.width(3), .mode("unsigned")) comparator_6 (.a(WA), .b(3'b101), .gt(n52), .eq(n53), .lt(n54));
  and and_6 (n55, WE, n53);
  Multiplexer #(.width(8), .select(1), .enable("false")) multiplexer_6 (
    .in0(WD), .in1({8{1'b0}}), .out(n57), .sel(RST));
  or or_6 (n58, RST, n55);
  Register #(.width(8), .trigger("falling"), .Select("high")) register_6 (
    .D(n57), .en(n58), .Q(n56), .clk(CLK), .clr(1'b0), .cs(1'b1), .preset(1'b0));
  Comparator #(.width(3), .mode("unsigned")) comparator_7 (.a(WA), .b(3'b110), .gt(n60), .eq(n61), .lt(n62));
  and and_7 (n63, WE, n61);
  Multiplexer #(.width(8), .select(1), .enable("false")) multiplexer_7 (
    .in0(WD), .in1({8{1'b0}}), .out(n65), .sel(RST));
  or or_7 (n66, RST, n63);
  Register #(.width(8), .trigger("falling"), .Select("high")) register_7 (
    .D(n65), .en(n66), .Q(n64), .clk(CLK), .clr(1'b0), .cs(1'b1), .preset(1'b0));
  Comparator #(.width(3), .mode("unsigned")) comparator_8 (.a(WA), .b(3'b111), .gt(n68), .eq(n69), .lt(n70));
  and and_8 (n71, WE, n69);
  Multiplexer #(.width(8), .select(1), .enable("false")) multiplexer_8 (
    .in0(WD), .in1({8{1'b0}}), .out(n73), .sel(RST));
  or or_8 (n74, RST, n71);
  Register #(.width(8), .trigger("falling"), .Select("high")) register_8 (
    .D(n73), .en(n74), .Q(n72), .clk(CLK), .clr(1'b0), .cs(1'b1), .preset(1'b0));
  Multiplexer #(.width(8), .select(1), .enable("false")) multiplexer_9 (.in0(n15), .in1(n24), .out(n78), .sel(RA[0]));
  Multiplexer #(.width(8), .select(1), .enable("false")) multiplexer_10 (.in0(n32), .in1(n40), .out(n79), .sel(RA[0]));
  Multiplexer #(.width(8), .select(1), .enable("false")) multiplexer_11 (.in0(n48), .in1(n56), .out(n80), .sel(RA[0]));
  Multiplexer #(.width(8), .select(1), .enable("false")) multiplexer_12 (.in0(n64), .in1(n72), .out(n81), .sel(RA[0]));
  Multiplexer #(.width(8), .select(1), .enable("false")) multiplexer_13 (.in0(n78), .in1(n79), .out(n82), .sel(RA[1]));
  Multiplexer #(.width(8), .select(1), .enable("false")) multiplexer_14 (.in0(n80), .in1(n81), .out(n83), .sel(RA[1]));
  Multiplexer #(.width(8), .select(1), .enable("false")) multiplexer_15 (.in0(n82), .in1(n83), .out(QA), .sel(RA[2]));
  Multiplexer #(.width(8), .select(1), .enable("false")) multiplexer_16 (.in0(n15), .in1(n24), .out(n88), .sel(RB[0]));
  Multiplexer #(.width(8), .select(1), .enable("false")) multiplexer_17 (.in0(n32), .in1(n40), .out(n89), .sel(RB[0]));
  Multiplexer #(.width(8), .select(1), .enable("false")) multiplexer_18 (.in0(n48), .in1(n56), .out(n90), .sel(RB[0]));
  Multiplexer #(.width(8), .select(1), .enable("false")) multiplexer_19 (.in0(n64), .in1(n72), .out(n91), .sel(RB[0]));
  Multiplexer #(.width(8), .select(1), .enable("false")) multiplexer_20 (.in0(n88), .in1(n89), .out(n92), .sel(RB[1]));
  Multiplexer #(.width(8), .select(1), .enable("false")) multiplexer_21 (.in0(n90), .in1(n91), .out(n93), .sel(RB[1]));
  Multiplexer #(.width(8), .select(1), .enable("false")) multiplexer_22 (.in0(n92), .in1(n93), .out(QB), .sel(RB[2]));

  // Other names for the same wires on the sheet: n84[7:0] = QA; n94[7:0] = QB; n75 = RA[0]; n76 = RA[1]; n77 = RA[2];
  //   n85 = RB[0]; n86 = RB[1]; n87 = RB[2]
endmodule
