// Logisim project ignores-write-enable.circ as structural Verilog: 1 circuit, main circuit main
module main (
  input  CLK,
  input  RST,
  input  WE,
  input  [2:0] WA,
  input  [7:0] WD,
  input  [2:0] RA,
  input  [2:0] RB,
  output [7:0] QB,
  output [7:0] QA
);

  wire n9, n10, n11, n17, n19, n20, n21, n24, n26, n27, n28, n31, n33, n34, n35, n38, n40, n41, n42, n45,
       n47, n48, n49, n52, n54, n55, n56, n59, n61, n62, n63, n66;
  wire [7:0] n14, n16, n22, n23, n29, n30, n36, n37, n43, n44, n50, n51, n57, n58, n64, n65, n70, n71, n72,
       n73, n74, n75, n80, n81, n82, n83, n84, n85;

  Comparator #(.width(3), .mode("unsigned")) comparator_1 (.a(WA), .b(3'b000), .gt(n9), .eq(n10), .lt(n11));
  Multiplexer #(.width(8), .select(1), .enable("false")) multiplexer_1 (
    .in0(WD), .in1({8{1'b0}}), .out(n16), .sel(RST));
  or or_1 (n17, RST, n10);
  Register #(.width(8), .trigger("rising"), .Select("high")) register_1 (
    .D(n16), .en(n17), .Q(n14), .clk(CLK), .clr(1'b0), .cs(1'b1), .preset(1'b0));
  Comparator #(.width(3), .mode("unsigned")) comparator_2 (.a(WA), .b(3'b001), .gt(n19), .eq(n20), .lt(n21));
  Multiplexer #(.width(8), .select(1), .enable("false")) multiplexer_2 (
    .in0(WD), .in1({8{1'b0}}), .out(n23), .sel(RST));
  or or_2 (n24, RST, n20);
  Register #(.width(8), .trigger("rising"), .Select("high")) register_2 (
    .D(n23), .en(n24), .Q(n22), .clk(CLK), .clr(1'b0), .cs(1'b1), .preset(1'b0));
  Comparator #(.width(3), .mode("unsigned")) comparator_3 (.a(WA), .b(3'b010), .gt(n26), .eq(n27), .lt(n28));
  Multiplexer #(.width(8), .select(1), .enable("false")) multiplexer_3 (
    .in0(WD), .in1({8{1'b0}}), .out(n30), .sel(RST));
  or or_3 (n31, RST, n27);
  Register #(.width(8), .trigger("rising"), .Select("high")) register_3 (
    .D(n30), .en(n31), .Q(n29), .clk(CLK), .clr(1'b0), .cs(1'b1), .preset(1'b0));
  Comparator #(.width(3), .mode("unsigned")) comparator_4 (.a(WA), .b(3'b011), .gt(n33), .eq(n34), .lt(n35));
  Multiplexer #(.width(8), .select(1), .enable("false")) multiplexer_4 (
    .in0(WD), .in1({8{1'b0}}), .out(n37), .sel(RST));
  or or_4 (n38, RST, n34);
  Register #(.width(8), .trigger("rising"), .Select("high")) register_4 (
    .D(n37), .en(n38), .Q(n36), .clk(CLK), .clr(1'b0), .cs(1'b1), .preset(1'b0));
  Comparator #(.width(3), .mode("unsigned")) comparator_5 (.a(WA), .b(3'b100), .gt(n40), .eq(n41), .lt(n42));
  Multiplexer #(.width(8), .select(1), .enable("false")) multiplexer_5 (
    .in0(WD), .in1({8{1'b0}}), .out(n44), .sel(RST));
  or or_5 (n45, RST, n41);
  Register #(.width(8), .trigger("rising"), .Select("high")) register_5 (
    .D(n44), .en(n45), .Q(n43), .clk(CLK), .clr(1'b0), .cs(1'b1), .preset(1'b0));
  Comparator #(.width(3), .mode("unsigned")) comparator_6 (.a(WA), .b(3'b101), .gt(n47), .eq(n48), .lt(n49));
  Multiplexer #(.width(8), .select(1), .enable("false")) multiplexer_6 (
    .in0(WD), .in1({8{1'b0}}), .out(n51), .sel(RST));
  or or_6 (n52, RST, n48);
  Register #(.width(8), .trigger("rising"), .Select("high")) register_6 (
    .D(n51), .en(n52), .Q(n50), .clk(CLK), .clr(1'b0), .cs(1'b1), .preset(1'b0));
  Comparator #(.width(3), .mode("unsigned")) comparator_7 (.a(WA), .b(3'b110), .gt(n54), .eq(n55), .lt(n56));
  Multiplexer #(.width(8), .select(1), .enable("false")) multiplexer_7 (
    .in0(WD), .in1({8{1'b0}}), .out(n58), .sel(RST));
  or or_7 (n59, RST, n55);
  Register #(.width(8), .trigger("rising"), .Select("high")) register_7 (
    .D(n58), .en(n59), .Q(n57), .clk(CLK), .clr(1'b0), .cs(1'b1), .preset(1'b0));
  Comparator #(.width(3), .mode("unsigned")) comparator_8 (.a(WA), .b(3'b111), .gt(n61), .eq(n62), .lt(n63));
  Multiplexer #(.width(8), .select(1), .enable("false")) multiplexer_8 (
    .in0(WD), .in1({8{1'b0}}), .out(n65), .sel(RST));
  or or_8 (n66, RST, n62);
  Register #(.width(8), .trigger("rising"), .Select("high")) register_8 (
    .D(n65), .en(n66), .Q(n64), .clk(CLK), .clr(1'b0), .cs(1'b1), .preset(1'b0));
  Multiplexer #(.width(8), .select(1), .enable("false")) multiplexer_9 (.in0(n14), .in1(n22), .out(n70), .sel(RA[0]));
  Multiplexer #(.width(8), .select(1), .enable("false")) multiplexer_10 (.in0(n29), .in1(n36), .out(n71), .sel(RA[0]));
  Multiplexer #(.width(8), .select(1), .enable("false")) multiplexer_11 (.in0(n43), .in1(n50), .out(n72), .sel(RA[0]));
  Multiplexer #(.width(8), .select(1), .enable("false")) multiplexer_12 (.in0(n57), .in1(n64), .out(n73), .sel(RA[0]));
  Multiplexer #(.width(8), .select(1), .enable("false")) multiplexer_13 (.in0(n70), .in1(n71), .out(n74), .sel(RA[1]));
  Multiplexer #(.width(8), .select(1), .enable("false")) multiplexer_14 (.in0(n72), .in1(n73), .out(n75), .sel(RA[1]));
  Multiplexer #(.width(8), .select(1), .enable("false")) multiplexer_15 (.in0(n74), .in1(n75), .out(QA), .sel(RA[2]));
  Multiplexer #(.width(8), .select(1), .enable("false")) multiplexer_16 (.in0(n14), .in1(n22), .out(n80), .sel(RB[0]));
  Multiplexer #(.width(8), .select(1), .enable("false")) multiplexer_17 (.in0(n29), .in1(n36), .out(n81), .sel(RB[0]));
  Multiplexer #(.width(8), .select(1), .enable("false")) multiplexer_18 (.in0(n43), .in1(n50), .out(n82), .sel(RB[0]));
  Multiplexer #(.width(8), .select(1), .enable("false")) multiplexer_19 (.in0(n57), .in1(n64), .out(n83), .sel(RB[0]));
  Multiplexer #(.width(8), .select(1), .enable("false")) multiplexer_20 (.in0(n80), .in1(n81), .out(n84), .sel(RB[1]));
  Multiplexer #(.width(8), .select(1), .enable("false")) multiplexer_21 (.in0(n82), .in1(n83), .out(n85), .sel(RB[1]));
  Multiplexer #(.width(8), .select(1), .enable("false")) multiplexer_22 (.in0(n84), .in1(n85), .out(QB), .sel(RB[2]));

  // Other names for the same wires on the sheet: n76[7:0] = QA; n86[7:0] = QB; n67 = RA[0]; n68 = RA[1]; n69 = RA[2];
  //   n77 = RB[0]; n78 = RB[1]; n79 = RB[2]
endmodule
