// Logisim project signed-order.circ as structural Verilog: 1 circuit, main circuit main
module main (
  input  [7:0] X0,
  input  [7:0] X1,
  input  [7:0] X2,
  input  [7:0] X3,
  input  [7:0] X4,
  input  [7:0] X5,
  input  [7:0] X6,
  input  [7:0] X7,
  output [7:0] Y4,
  output [7:0] Y5,
  output [7:0] Y6,
  output [7:0] Y7,
  output [7:0] Y0,
  output [7:0] Y1,
  output [7:0] Y2,
  output [7:0] Y3
);

  wire n9, n10, n11, n14, n15, n16, n19, n20, n21, n24, n25, n26, n29, n30, n31, n34, n35, n36, n39, n40,
       n41, n44, n45, n46, n49, n50, n51, n54, n55, n56, n59, n60, n61, n64, n65, n66, n69, n70, n71, n74,
       n75, n76, n79, n80, n81, n84, n85, n86, n89, n90, n91, n94, n95, n96, n99, n100, n101, n104, n105,
       n106, n109, n110, n111, n114, n115, n116, n119, n120, n121, n124, n125, n126, n129, n130, n131, n134,
       n135, n136, n139, n140, n141, n144, n145, n146;
  wire [7:0] n12, n13, n17, n18, n22, n23, n27, n28, n32, n33, n37, n38, n42, n43, n47, n48, n52, n53, n57,
       n58, n62, n63, n67, n68, n72, n73, n77, n78, n82, n83, n87, n88, n92, n93, n97, n98, n102, n103, n107,
       n108, n112, n113, n118, n122, n123, n127, n128, n132;

  Comparator #(.width(8), .mode("twosComplement")) comparator_1 (.a(X0), .b(X1), .gt(n9), .eq(n10), .lt(n11));
  Multiplexer #(.width(8), .select(1), .enable("false")) multiplexer_1 (.in0(X0), .in1(X1), .out(n12), .sel(n9));
  Multiplexer #(.width(8), .select(1), .enable("false")) multiplexer_2 (.in0(X1), .in1(X0), .out(n13), .sel(n9));
  Comparator #(.width(8), .mode("twosComplement")) comparator_2 (.a(X2), .b(X3), .gt(n14), .eq(n15), .lt(n16));
  Multiplexer #(.width(8), .select(1), .enable("false")) multiplexer_3 (.in0(X2), .in1(X3), .out(n17), .sel(n14));
  Multiplexer #(.width(8), .select(1), .enable("false")) multiplexer_4 (.in0(X3), .in1(X2), .out(n18), .sel(n14));
  Comparator #(.width(8), .mode("twosComplement")) comparator_3 (.a(X4), .b(X5), .gt(n19), .eq(n20), .lt(n21));
  Multiplexer #(.width(8), .select(1), .enable("false")) multiplexer_5 (.in0(X4), .in1(X5), .out(n22), .sel(n19));
  Multiplexer #(.width(8), .select(1), .enable("false")) multiplexer_6 (.in0(X5), .in1(X4), .out(n23), .sel(n19));
  Comparator #(.width(8), .mode("twosComplement")) comparator_4 (.a(X6), .b(X7), .gt(n24), .eq(n25), .lt(n26));
  Multiplexer #(.width(8), .select(1), .enable("false")) multiplexer_7 (.in0(X6), .in1(X7), .out(n27), .sel(n24));
  Multiplexer #(.width(8), .select(1), .enable("false")) multiplexer_8 (.in0(X7), .in1(X6), .out(n28), .sel(n24));
  Comparator #(.width(8), .mode("twosComplement")) comparator_5 (.a(n13), .b(n17), .gt(n29), .eq(n30), .lt(n31));
  Multiplexer #(.width(8), .select(1), .enable("false")) multiplexer_9 (.in0(n13), .in1(n17), .out(n32), .sel(n29));
  Multiplexer #(.width(8), .select(1), .enable("false")) multiplexer_10 (.in0(n17), .in1(n13), .out(n33), .sel(n29));
  Comparator #(.width(8), .mode("twosComplement")) comparator_6 (.a(n18), .b(n22), .gt(n34), .eq(n35), .lt(n36));
  Multiplexer #(.width(8), .select(1), .enable("false")) multiplexer_11 (.in0(n18), .in1(n22), .out(n37), .sel(n34));
  Multiplexer #(.width(8), .select(1), .enable("false")) multiplexer_12 (.in0(n22), .in1(n18), .out(n38), .sel(n34));
  Comparator #(.width(8), .mode("twosComplement")) comparator_7 (.a(n23), .b(n27), .gt(n39), .eq(n40), .lt(n41));
  Multiplexer #(.width(8), .select(1), .enable("false")) multiplexer_13 (.in0(n23), .in1(n27), .out(n42), .sel(n39));
  Multiplexer #(.width(8), .select(1), .enable("false")) multiplexer_14 (.in0(n27), .in1(n23), .out(n43), .sel(n39));
  Comparator #(.width(8), .mode("twosComplement")) comparator_8 (.a(n12), .b(n32), .gt(n44), .eq(n45), .lt(n46));
  Multiplexer #(.width(8), .select(1), .enable("false")) multiplexer_15 (.in0(n12), .in1(n32), .out(n47), .sel(n44));
  Multiplexer #(.width(8), .select(1), .enable("false")) multiplexer_16 (.in0(n32), .in1(n12), .out(n48), .sel(n44));
  Comparator #(.width(8), .mode("twosComplement")) comparator_9 (.a(n33), .b(n37), .gt(n49), .eq(n50), .lt(n51));
  Multiplexer #(.width(8), .select(1), .enable("false")) multiplexer_17 (.in0(n33), .in1(n37), .out(n52), .sel(n49));
  Multiplexer #(.width(8), .select(1), .enable("false")) multiplexer_18 (.in0(n37), .in1(n33), .out(n53), .sel(n49));
  Comparator #(.width(8), .mode("twosComplement")) comparator_10 (.a(n38), .b(n42), .gt(n54), .eq(n55), .lt(n56));
  Multiplexer #(.width(8), .select(1), .enable("false")) multiplexer_19 (.in0(n38), .in1(n42), .out(n57), .sel(n54));
  Multiplexer #(.width(8), .select(1), .enable("false")) multiplexer_20 (.in0(n42), .in1(n38), .out(n58), .sel(n54));
  Comparator #(.width(8), .mode("twosComplement")) comparator_11 (.a(n43), .b(n28), .gt(n59), .eq(n60), .lt(n61));
  Multiplexer #(.width(8), .select(1), .enable("false")) multiplexer_21 (.in0(n43), .in1(n28), .out(n62), .sel(n59));
  Multiplexer #(.width(8), .select(1), .enable("false")) multiplexer_22 (.in0(n28), .in1(n43), .out(n63), .sel(n59));
  Comparator #(.width(8), .mode("twosComplement")) comparator_12 (.a(n48), .b(n52), .gt(n64), .eq(n65), .lt(n66));
  Multiplexer #(.width(8), .select(1), .enable("false")) multiplexer_23 (.in0(n48), .in1(n52), .out(n67), .sel(n64));
  Multiplexer #(.width(8), .select(1), .enable("false")) multiplexer_24 (.in0(n52), .in1(n48), .out(n68), .sel(n64));
  Comparator #(.width(8), .mode("twosComplement")) comparator_13 (.a(n53), .b(n57), .gt(n69), .eq(n70), .lt(n71));
  Multiplexer #(.width(8), .select(1), .enable("false")) multiplexer_25 (.in0(n53), .in1(n57), .out(n72), .sel(n69));
  Multiplexer #(.width(8), .select(1), .enable("false")) multiplexer_26 (.in0(n57), .in1(n53), .out(n73), .sel(n69));
  Comparator #(.width(8), .mode("twosComplement")) comparator_14 (.a(n58), .b(n62), .gt(n74), .eq(n75), .lt(n76));
  Multiplexer #(.width(8), .select(1), .enable("false")) multiplexer_27 (.in0(n58), .in1(n62), .out(n77), .sel(n74));
  Multiplexer #(.width(8), .select(1), .enable("false")) multiplexer_28 (.in0(n62), .in1(n58), .out(n78), .sel(n74));
  Comparator #(.width(8), .mode("twosComplement")) comparator_15 (.a(n47), .b(n67), .gt(n79), .eq(n80), .lt(n81));
  Multiplexer #(.width(8), .select(1), .enable("false")) multiplexer_29 (.in0(n47), .in1(n67), .out(n82), .sel(n79));
  Multiplexer #(.width(8), .select(1), .enable("false")) multiplexer_30 (.in0(n67), .in1(n47), .out(n83), .sel(n79));
  Comparator #(.width(8), .mode("twosComplement")) comparator_16 (.a(n68), .b(n72), .gt(n84), .eq(n85), .lt(n86));
  Multiplexer #(.width(8), .select(1), .enable("false")) multiplexer_31 (.in0(n68), .in1(n72), .out(n87), .sel(n84));
  Multiplexer #(.width(8), .select(1), .enable("false")) multiplexer_32 (.in0(n72), .in1(n68), .out(n88), .sel(n84));
  Comparator #(.width(8), .mode("twosComplement")) comparator_17 (.a(n73), .b(n77), .gt(n89), .eq(n90), .lt(n91));
  Multiplexer #(.width(8), .select(1), .enable("false")) multiplexer_33 (.in0(n73), .in1(n77), .out(n92), .sel(n89));
  Multiplexer #(.width(8), .select(1), .enable("false")) multiplexer_34 (.in0(n77), .in1(n73), .out(n93), .sel(n89));
  Comparator #(.width(8), .mode("twosComplement")) comparator_18 (.a(n78), .b(n63), .gt(n94), .eq(n95), .lt(n96));
  Multiplexer #(.width(8), .select(1), .enable("false")) multiplexer_35 (.in0(n78), .in1(n63), .out(n97), .sel(n94));
  Multiplexer #(.width(8), .select(1), .enable("false")) multiplexer_36 (.in0(n63), .in1(n78), .out(n98), .sel(n94));
  Comparator #(.width(8), .mode("twosComplement")) comparator_19 (.a(n83), .b(n87), .gt(n99), .eq(n100), .lt(n101));
  Multiplexer #(.width(8), .select(1), .enable("false")) multiplexer_37 (.in0(n83), .in1(n87), .out(n102), .sel(n99));
  Multiplexer #(.width(8), .select(1), .enable("false")) multiplexer_38 (.in0(n87), .in1(n83), .out(n103), .sel(n99));
  Comparator #(.width(8), .mode("twosComplement")) comparator_20 (.a(n88), .b(n92), .gt(n104), .eq(n105), .lt(n106));
  Multiplexer #(.width(8), .select(1), .enable("false")) multiplexer_39 (.in0(n88), .in1(n92), .out(n107), .sel(n104));
  Multiplexer #(.width(8), .select(1), .enable("false")) multiplexer_40 (.in0(n92), .in1(n88), .out(n108), .sel(n104));
  Comparator #(.width(8), .mode("twosComplement")) comparator_21 (.a(n93), .b(n97), .gt(n109), .eq(n110), .lt(n111));
  Multiplexer #(.width(8), .select(1), .enable("false")) multiplexer_41 (.in0(n93), .in1(n97), .out(n112), .sel(n109));
  Multiplexer #(.width(8), .select(1), .enable("false")) multiplexer_42 (.in0(n97), .in1(n93), .out(n113), .sel(n109));
  Comparator #(.width(8), .mode("twosComplement")) comparator_22 (.a(n82), .b(n102), .gt(n114), .eq(n115), .lt(n116));
  Multiplexer #(.width(8), .select(1), .enable("false")) multiplexer_43 (.in0(n82), .in1(n102), .out(Y0), .sel(n114));
  Multiplexer #(.width(8), .select(1), .enable("false")) multiplexer_44 (.in0(n102), .in1(n82), .out(n118), .sel(n114));
  Comparator #(.width(8), .mode("twosComplement")) comparator_23 (.a(n103), .b(n107), .gt(n119), .eq(n120), .lt(n121));
  Multiplexer #(.width(8), .select(1), .enable("false")) multiplexer_45 (
    .in0(n103), .in1(n107), .out(n122), .sel(n119));
  Multiplexer #(.width(8), .select(1), .enable("false")) multiplexer_46 (
    .in0(n107), .in1(n103), .out(n123), .sel(n119));
  Comparator #(.width(8), .mode("twosComplement")) comparator_24 (.a(n108), .b(n112), .gt(n124), .eq(n125), .lt(n126));
  Multiplexer #(.width(8), .select(1), .enable("false")) multiplexer_47 (
    .in0(n108), .in1(n112), .out(n127), .sel(n124));
  Multiplexer #(.width(8), .select(1), .enable("false")) multiplexer_48 (
    .in0(n112), .in1(n108), .out(n128), .sel(n124));
  Comparator #(.width(8), .mode("twosComplement")) comparator_25 (.a(n113), .b(n98), .gt(n129), .eq(n130), .lt(n131));
  Multiplexer #(.width(8), .select(1), .enable("false")) multiplexer_49 (.in0(n113), .in1(n98), .out(n132), .sel(n129));
  Multiplexer #(.width(8), .select(1), .enable("false")) multiplexer_50 (.in0(n98), .in1(n113), .out(Y7), .sel(n129));
  Comparator #(.width(8), .mode("twosComplement")) comparator_26 (.a(n118), .b(n122), .gt(n134), .eq(n135), .lt(n136));
  Multiplexer #(.width(8), .select(1), .enable("false")) multiplexer_51 (.in0(n118), .in1(n122), .out(Y1), .sel(n134));
  Multiplexer #(.width(8), .select(1), .enable("false")) multiplexer_52 (.in0(n122), .in1(n118), .out(Y2), .sel(n134));
  Comparator #(.width(8), .mode("twosComplement")) comparator_27 (.a(n123), .b(n127), .gt(n139), .eq(n140), .lt(n141));
  Multiplexer #(.width(8), .select(1), .enable("false")) multiplexer_53 (.in0(n123), .in1(n127), .out(Y3), .sel(n139));
  Multiplexer #(.width(8), .select(1), .enable("false")) multiplexer_54 (.in0(n127), .in1(n123), .out(Y4), .sel(n139));
  Comparator #(.width(8), .mode("twosComplement")) comparator_28 (.a(n128), .b(n132), .gt(n144), .eq(n145), .lt(n146));
  Multiplexer #(.width(8), .select(1), .enable("false")) multiplexer_55 (.in0(n128), .in1(n132), .out(Y5), .sel(n144));
  Multiplexer #(.width(8), .select(1), .enable("false")) multiplexer_56 (.in0(n132), .in1(n128), .out(Y6), .sel(n144));

  // Other names for the same wires on the sheet: n117[7:0] = Y0; n133[7:0] = Y7; n137[7:0] = Y1; n138[7:0] = Y2;
  //   n142[7:0] = Y3; n143[7:0] = Y4; n147[7:0] = Y5; n148[7:0] = Y6
endmodule
